// Logisim project Clock12H.circ as structural Verilog: 4 circuits, main circuit main
module main (
);

  wire and_2_out, and_3_out, and_4_out, and_5_out, and_6_out, clock_1_out, counter0_9_1_a0, counter0_9_1_a1,
       counter0_9_1_a2, counter0_9_1_a3, counter0_9_2_a0, counter0_9_2_a1, counter0_9_2_a2, counter0_9_2_a3,
       counter0_9_2_y, counter0_9_3_a0, counter0_9_3_a1, counter0_9_3_a2, counter0_9_3_a3, counter0_9_3_y,
       counter_0_5_1_a0, counter_0_5_1_a1, counter_0_5_1_a2, counter_0_5_1_y, counter_0_5_2_a0,
       counter_0_5_2_a1, counter_0_5_2_a2, counter_0_5_2_y, d_flip_flop_1_p1, d_flip_flop_1_p2,
       d_flip_flop_1_p3, d_flip_flop_1_p4, n7448_1__9__e, n7448_1__10__d, n7448_1__11__c, n7448_1__12__b,
       n7448_1__13__a, n7448_1__14__g, n7448_1__15__f, n7448_2__9__e, n7448_2__10__d, n7448_2__11__c,
       n7448_2__12__b, n7448_2__13__a, n7448_2__14__g, n7448_2__15__f, n7448_3__9__e, n7448_3__10__d,
       n7448_3__11__c, n7448_3__12__b, n7448_3__13__a, n7448_3__14__g, n7448_3__15__f, n7448_4__9__e,
       n7448_4__10__d, n7448_4__11__c, n7448_4__12__b, n7448_4__13__a, n7448_4__14__g, n7448_4__15__f,
       n7448_5__9__e, n7448_5__10__d, n7448_5__11__c, n7448_5__12__b, n7448_5__13__a, n7448_5__14__g,
       n7448_5__15__f, n7448_6__9__e, n7448_6__10__d, n7448_6__11__c, n7448_6__12__b, n7448_6__13__a,
       n7448_6__14__g, n7448_6__15__f;

  // D_Flip_Flop d_flip_flop_1: pin names not known; wires that end beside it: d_flip_flop_1_p1, d_flip_flop_1_p2, d_flip_flop_1_p3, d_flip_flop_1_p4, d_flip_flop_1_p1
  _7_Segment_Display u_7_segment_display_1 (
    .g(n7448_1__14__g), .f(n7448_1__15__f), .a(n7448_1__13__a), .b(n7448_1__12__b), .e(n7448_1__9__e),
    .d(n7448_1__10__d), .c(n7448_1__11__c));  // open: dp
  and and_1 (d_flip_flop_1_p3, counter0_9_1_a0, counter0_9_1_a1);
  _7448 u_7448_1 (
    ._1__B(1'b0), ._2__C(1'b0), ._3__nLT(1'b1), ._4__NC(1'b1), ._5__nRBI(1'b1), ._6__D(1'b0),
    ._7__A(d_flip_flop_1_p4), ._15__f(n7448_1__15__f), ._14__g(n7448_1__14__g), ._13__a(n7448_1__13__a),
    ._12__b(n7448_1__12__b), ._11__c(n7448_1__11__c), ._10__d(n7448_1__10__d), ._9__e(n7448_1__9__e));  // open: _8__GND, _16__Vcc
  and and_2 (and_2_out, counter0_9_1_a0, counter0_9_1_a1, d_flip_flop_1_p4);
  counter0_9 counter0_9_1 (
    .Clock(and_3_out), .A3(counter0_9_1_a3), .A2(counter0_9_1_a2), .A1(counter0_9_1_a1),
    .A0(counter0_9_1_a0), .Y(d_flip_flop_1_p2), .Reset(and_2_out));
  _7448 u_7448_2 (
    ._1__B(counter0_9_1_a1), ._2__C(counter0_9_1_a2), ._3__nLT(1'b1), ._4__NC(1'b1), ._5__nRBI(1'b1),
    ._6__D(counter0_9_1_a3), ._7__A(counter0_9_1_a0), ._15__f(n7448_2__15__f), ._14__g(n7448_2__14__g),
    ._13__a(n7448_2__13__a), ._12__b(n7448_2__12__b), ._11__c(n7448_2__11__c), ._10__d(n7448_2__10__d),
    ._9__e(n7448_2__9__e));  // open: _8__GND, _16__Vcc
  _7_Segment_Display u_7_segment_display_2 (
    .g(n7448_2__14__g), .f(n7448_2__15__f), .a(n7448_2__13__a), .b(n7448_2__12__b), .e(n7448_2__9__e),
    .d(n7448_2__10__d), .c(n7448_2__11__c));  // open: dp
  and and_3 (and_3_out, clock_1_out, counter_0_5_1_y);
  and and_4 (and_4_out, clock_1_out, counter0_9_2_y);
  counter_0_5 counter_0_5_1 (
    .A2(counter_0_5_1_a2), .A1(counter_0_5_1_a1), .A0(counter_0_5_1_a0), .in_2(and_4_out), .Reset(and_2_out),
    .Y(counter_0_5_1_y));
  _7448 u_7448_3 (
    ._1__B(counter_0_5_1_a1), ._2__C(counter_0_5_1_a2), ._3__nLT(1'b1), ._4__NC(1'b1), ._5__nRBI(1'b1),
    ._6__D(1'b0), ._7__A(counter_0_5_1_a0), ._15__f(n7448_3__15__f), ._14__g(n7448_3__14__g),
    ._13__a(n7448_3__13__a), ._12__b(n7448_3__12__b), ._11__c(n7448_3__11__c), ._10__d(n7448_3__10__d),
    ._9__e(n7448_3__9__e));  // open: _8__GND, _16__Vcc
  _7_Segment_Display u_7_segment_display_3 (
    .g(n7448_3__14__g), .f(n7448_3__15__f), .a(n7448_3__13__a), .b(n7448_3__12__b), .e(n7448_3__9__e),
    .d(n7448_3__10__d), .c(n7448_3__11__c));  // open: dp
  counter0_9 counter0_9_2 (
    .Clock(and_5_out), .A3(counter0_9_2_a3), .A2(counter0_9_2_a2), .A1(counter0_9_2_a1),
    .A0(counter0_9_2_a0), .Y(counter0_9_2_y), .Reset(and_2_out));
  _7448 u_7448_4 (
    ._1__B(counter0_9_2_a1), ._2__C(counter0_9_2_a2), ._3__nLT(1'b1), ._4__NC(1'b1), ._5__nRBI(1'b1),
    ._6__D(counter0_9_2_a3), ._7__A(counter0_9_2_a0), ._15__f(n7448_4__15__f), ._14__g(n7448_4__14__g),
    ._13__a(n7448_4__13__a), ._12__b(n7448_4__12__b), ._11__c(n7448_4__11__c), ._10__d(n7448_4__10__d),
    ._9__e(n7448_4__9__e));  // open: _8__GND, _16__Vcc
  _7_Segment_Display u_7_segment_display_4 (
    .g(n7448_4__14__g), .f(n7448_4__15__f), .a(n7448_4__13__a), .b(n7448_4__12__b), .e(n7448_4__9__e),
    .d(n7448_4__10__d), .c(n7448_4__11__c));  // open: dp
  and and_5 (and_5_out, clock_1_out, counter_0_5_2_y);
  counter_0_5 counter_0_5_2 (
    .A2(counter_0_5_2_a2), .A1(counter_0_5_2_a1), .A0(counter_0_5_2_a0), .in_2(and_6_out), .Reset(and_2_out),
    .Y(counter_0_5_2_y));
  _7448 u_7448_5 (
    ._1__B(counter_0_5_2_a1), ._2__C(counter_0_5_2_a2), ._3__nLT(1'b1), ._4__NC(1'b1), ._5__nRBI(1'b1),
    ._6__D(1'b0), ._7__A(counter_0_5_2_a0), ._15__f(n7448_5__15__f), ._14__g(n7448_5__14__g),
    ._13__a(n7448_5__13__a), ._12__b(n7448_5__12__b), ._11__c(n7448_5__11__c), ._10__d(n7448_5__10__d),
    ._9__e(n7448_5__9__e));  // open: _8__GND, _16__Vcc
  _7_Segment_Display u_7_segment_display_5 (
    .g(n7448_5__14__g), .f(n7448_5__15__f), .a(n7448_5__13__a), .b(n7448_5__12__b), .e(n7448_5__9__e),
    .d(n7448_5__10__d), .c(n7448_5__11__c));  // open: dp
  and and_6 (and_6_out, clock_1_out, counter0_9_3_y);
  counter0_9 counter0_9_3 (
    .Clock(clock_1_out), .A3(counter0_9_3_a3), .A2(counter0_9_3_a2), .A1(counter0_9_3_a1),
    .A0(counter0_9_3_a0), .Y(counter0_9_3_y), .Reset(and_2_out));
  _7448 u_7448_6 (
    ._1__B(counter0_9_3_a1), ._2__C(counter0_9_3_a2), ._3__nLT(1'b1), ._4__NC(1'b1), ._5__nRBI(1'b1),
    ._6__D(counter0_9_3_a3), ._7__A(counter0_9_3_a0), ._15__f(n7448_6__15__f), ._14__g(n7448_6__14__g),
    ._13__a(n7448_6__13__a), ._12__b(n7448_6__12__b), ._11__c(n7448_6__11__c), ._10__d(n7448_6__10__d),
    ._9__e(n7448_6__9__e));  // open: _8__GND, _16__Vcc
  _7_Segment_Display u_7_segment_display_6 (
    .g(n7448_6__14__g), .f(n7448_6__15__f), .a(n7448_6__13__a), .b(n7448_6__12__b), .e(n7448_6__9__e),
    .d(n7448_6__10__d), .c(n7448_6__11__c));  // open: dp
  Clock clock_1 (.out(clock_1_out));
endmodule

module counter_0_5 (
  input  Reset,
  input  in_2,
  output A2,
  output A1,
  output A0,
  output Y
);

  wire and_1_out, and_2_out, and_3_out, and_4_out, and_5_out, and_6_out, d_flip_flop_1_p3, d_flip_flop_1_p5,
       d_flip_flop_2_p5, d_flip_flop_3_p5, or_1_out, or_2_out, or_3_out;

  and and_1 (and_1_out, A1, A0);
  and and_2 (and_2_out, A2, d_flip_flop_2_p5);
  and and_3 (and_3_out, d_flip_flop_1_p5, A1, d_flip_flop_3_p5);
  and and_4 (and_4_out, d_flip_flop_2_p5, A0);
  and and_5 (and_5_out, d_flip_flop_1_p5, d_flip_flop_3_p5);
  and and_6 (and_6_out, d_flip_flop_2_p5, d_flip_flop_3_p5);
  and u_Y (Y, A2, d_flip_flop_3_p5, A1);
  or or_1 (or_1_out, and_1_out, and_2_out);
  or or_2 (or_2_out, and_3_out, and_4_out);
  or or_3 (or_3_out, and_5_out, and_6_out);
  // D_Flip_Flop d_flip_flop_1: pin names not known; wires that end beside it: or_1_out, in_2, d_flip_flop_1_p3, A2, d_flip_flop_1_p5
  // D_Flip_Flop d_flip_flop_2: pin names not known; wires that end beside it: or_2_out, in_2, d_flip_flop_1_p3, A1, d_flip_flop_2_p5
  // D_Flip_Flop d_flip_flop_3: pin names not known; wires that end beside it: or_3_out, in_2, d_flip_flop_1_p3, A0, d_flip_flop_3_p5
  or or_4 (d_flip_flop_1_p3, Y, Reset);
endmodule

module counter0_9 (
  input  Reset,
  input  Clock,
  output A3,
  output A2,
  output A1,
  output A0,
  output Y
);

  wire and_2_out, and_3_out, and_4_out, and_5_out, and_6_out, and_7_out, d_flip_flop_1_p4, d_flip_flop_2_p3,
       d_flip_flop_2_p6, d_flip_flop_3_p5, d_flip_flop_4_p1, or_1_out, or_2_out, or_3_out;

  and and_1 (Y, A3, d_flip_flop_2_p6, A1, d_flip_flop_4_p1);
  and and_2 (and_2_out, A2, A1, A0);
  and and_3 (and_3_out, d_flip_flop_2_p6, A1, A0);
  and and_4 (and_4_out, A2, d_flip_flop_3_p5);
  and and_5 (and_5_out, A2, d_flip_flop_4_p1);
  and and_6 (and_6_out, d_flip_flop_3_p5, A0);
  and and_7 (and_7_out, A1, d_flip_flop_4_p1);
  or or_1 (or_1_out, and_2_out, A3);
  or or_2 (or_2_out, and_3_out, and_4_out, and_5_out);
  or or_3 (or_3_out, and_6_out, and_7_out);
  // D_Flip_Flop d_flip_flop_1: pin names not known; wires that end beside it: or_1_out, Clock, A3, d_flip_flop_1_p4
  // D_Flip_Flop d_flip_flop_2: pin names not known; wires that end beside it: or_2_out, Clock, d_flip_flop_2_p3, d_flip_flop_2_p3, A2, d_flip_flop_2_p6
  // D_Flip_Flop d_flip_flop_3: pin names not known; wires that end beside it: or_3_out, Clock, d_flip_flop_2_p3, A1, d_flip_flop_3_p5
  // D_Flip_Flop d_flip_flop_4: pin names not known; wires that end beside it: d_flip_flop_4_p1, Clock, d_flip_flop_2_p3, A0, d_flip_flop_4_p1
  or or_4 (d_flip_flop_2_p3, Y, Reset);
endmodule

module BCD_7_seg (
  input  A,
  input  B,
  input  C,
  input  D,
  output A_2,
  output B_2,
  output C_2,
  output D_2,
  output E,
  output F,
  output G
);

  wire and_1_out, and_2_out, and_3_out, and_4_out, and_5_out, and_6_out, and_7_out, and_8_out, and_9_out,
       and_10_out, not_1_out, not_2_out, not_3_out, not_4_out, xnor_1_out, xnor_2_out, xor_1_out;

  not not_1 (not_1_out, A);
  not not_2 (not_2_out, B);
  not not_3 (not_3_out, C);
  not not_4 (not_4_out, D);
  xnor xnor_1 (xnor_1_out, B, D);
  xnor xnor_2 (xnor_2_out, C, D);
  and and_1 (and_1_out, not_2_out, not_4_out);
  and and_2 (and_2_out, not_2_out, C);
  and and_3 (and_3_out, B, not_3_out, D);
  and and_4 (and_4_out, C, not_4_out);
  and and_5 (and_5_out, not_3_out, not_4_out);
  and and_6 (and_6_out, B, not_3_out);
  and and_7 (and_7_out, B, not_4_out);
  and and_8 (and_8_out, B, not_4_out);
  or or_1 (A_2, xnor_1_out, C, A);
  or or_2 (B_2, xnor_2_out, not_2_out);
  or or_3 (C_2, not_3_out, D, B);
  and and_9 (and_9_out, not_2_out, not_4_out);
  and and_10 (and_10_out, C, not_4_out);
  xor xor_1 (xor_1_out, B, C);
  or or_4 (D_2, and_1_out, and_2_out, and_3_out, A, and_4_out);
  or or_5 (E, and_9_out, and_10_out);
  or or_6 (F, and_5_out, and_6_out, A, and_7_out);
  or or_7 (G, xor_1_out, and_8_out, A);
  _7_Segment_Display u_7_segment_display_1 (.g(G), .f(F), .a(A_2), .b(B_2), .e(E), .d(D_2), .c(C_2));  // open: dp
endmodule
