// Logisim project Libary.circ as structural Verilog: 89 circuits, main circuit main
module main (
);

  _7400 u_7400_1 ();  // open: _1__1A, _2__1B, _3__1Y, _4__2A, _5__2B, _6__2Y, _7__GND, _14__Vcc, _13__4B, _12__4A, _11__4Y, _10__3B, _9__3A, _8__3Y
  _7425 u_7425_1 ();  // open: _1__1A, _2__1B, _3__NC, _4__1C, _5__1D, _6__1Y, _7__GND, _14__Vcc, _13__2D, _12__2C, _11__NC, _10__2B, _9__2A, _8__2Y
  _7486 u_7486_1 ();  // open: _1__1A, _2__1B, _3__1Y, _4__2A, _5__2B, _6__2Y, _7__GND, _14__Vcc, _13__4B, _12__4A, _11__4Y, _10__3B, _9__3A, _8__3Y
  _74150 u_74150_1 ();  // open: _1__E7, _2__E6, _3__E5, _4__E4, _5__E3, _6__E2, _7__E1, _8__E0, _9__nG, _10__W, _11__D, _12__GND, _24__Vcc, _23__E8, _22__E9, _21__E10, _20__E11, _19__E12, _18__E13, _17__E14, _16__E15, _15__A, _14__B, _13__C
  _74174 u_74174_1 ();  // open: _1__MR_prime, _2__Q0, _3__D0, _4__D1, _5__Q1, _6__D2, _7__Q2, _8__GND, _16__Vcc, _15__Q5, _14__D5, _13__D4, _12__Q4, _11__D3, _10__Q3, _9__CP
  _744075 u_744075_1 ();  // open: _1__1A, _2__1B, _3__2A, _4__2B, _5__2C, _6__2Y, _7__GND, _14__Vcc, _13__1C, _12__1Y, _11__3C, _10__3B, _9__3A, _8__3Y
  _7402 u_7402_1 ();  // open: _1__1Y, _2__1A, _3__1B, _4__2Y, _5__2A, _6__2B, _7__GND, _14__Vcc, _13__4Y, _12__4B, _11__4A, _10__3Y, _9__3B, _8__3A
  _7427 u_7427_1 ();  // open: _1__1A, _2__1B, _3__2A, _4__2B, _5__2C, _6__2Y, _7__GND, _14__Vcc, _13__1C, _12__1Y, _11__3C, _10__3B, _9__3A, _8__3Y
  _7489 u_7489_1 ();  // open: _1__A0, _2__nCS, _3__nWE, _4__D1, _5__nO1, _6__D2, _7__nO2, _8__GND, _16__Vcc, _15__A1, _14__A2, _13__A3, _12__D4, _11__nO4, _10__D3, _9__nO3
  _7404 u_7404_1 ();  // open: _1__1A, _2__1Y, _3__2A, _4__2Y, _5__3A, _6__3Y, _7__GND, _14__Vcc, _13__6A, _12__6Y, _11__5A, _10__5Y, _9__4A, _8__4Y
  _7430 u_7430_1 ();  // open: _1__1A, _2__1B, _3__1C, _4__1D, _5__1E, _6__1F, _7__GND, _14__Vcc, _13__NC, _12__1H, _11__1G, _10__NC, _9__NC, _8__3Y
  _74151 u_74151_1 ();  // open: _1__D3, _2__D2, _3__D1, _4__D0, _5__Y, _6__W, _7__nG, _8__GND, _16__Vcc, _15__D4, _14__D5, _13__D6, _12__D7, _11__A, _10__B, _9__C
  _74198 u_74198_1 ();  // open: _1__S0, _2__Dsr, _3__P0, _4__Q0, _5__P1, _6__Q1, _7__P2, _8__Q2, _9__P3, _10__Q3, _11__CP, _12__GND, _24__Vcc, _23__S1, _22__Dsl, _21__P7, _20__Q7, _19__P6, _18__Q6, _17__P5, _16__Q5, _15__P4, _14__Q4, _13__nMR
  _7407 u_7407_1 ();  // open: _1__1A, _2__1Y, _3__2A, _4__2Y, _5__3A, _6__3Y, _7__GND, _14__Vcc, _13__6A, _12__6Y, _11__5A, _10__5Y, _9__4A, _8__4Y
  _7432 u_7432_1 ();  // open: _1__1A, _2__1B, _3__1Y, _4__2A, _5__2B, _6__2Y, _7__GND, _14__Vcc, _13__4B, _12__4A, _11__4Y, _10__3B, _9__3A, _8__3Y
  _74116 u_74116_1 ();  // open: _1__nMRa, _2__nE0a, _3__nE1a, _4__D0a, _5__Q0a, _6__D1a, _7__Q1a, _8__D2a, _9__Q2a, _10__D3a, _11__Q3a, _12__GND, _24__Vcc, _23__Q3b, _22__D3b, _21__Q2b, _20__D2b, _19__Q1b, _18__D1b, _17__Q0b, _16__D0b, _15__nE1b, _14__nE0b, _13__nMRb
  _74153 u_74153_1 ();  // open: _1__nG1, _2__B, _3__1C3, _4__1C2, _5__1C1, _6__1C0, _7__Y1, _8__GND, _16__Vcc, _15__nG2, _14__A, _13__2C3, _12__2C2, _11__2C1, _10__2C0, _9__Y2
  _74238 u_74238_1 ();  // open: _1__A0, _2__A1, _3__A2, _4__E1_prime, _5__E2_prime, _6__E3, _7__Y7, _8__GND, _16__Vcc, _15__Y0, _14__Y1, _13__Y2, _12__Y3, _11__Y4, _10__Y5, _9__Y6
  _7408 u_7408_1 ();  // open: _1__1A, _2__1B, _3__1Y, _4__2A, _5__2B, _6__2Y, _7__GND, _14__Vcc, _13__4B, _12__4A, _11__4Y, _10__3B, _9__3A, _8__3Y
  _7448 u_7448_1 ();  // open: _1__B, _2__C, _3__nLT, _4__NC, _5__nRBI, _6__D, _7__A, _8__GND, _16__Vcc, _15__f, _14__g, _13__a, _12__b, _11__c, _10__d, _9__e
  _74133 u_74133_1 ();  // open: _1__A, _2__B, _3__C, _4__D, _5__E, _6__F, _7__G, _8__GND, _16__Vcc, _15__M, _14__L, _13__K, _12__J, _11__I, _10__H, _9__Y
  _74253 u_74253_1 ();  // open: _1__1G, _2__Sb, _3__1C3, _4__1C2, _5__1C1, _6__1C0, _7__1Y, _8__GND, _16__Vcc, _15__2G, _14__Sa, _13__2C3, _12__2C2, _11__2C1, _10__2C0, _9__2Y
  _7410 u_7410_1 ();  // open: _1__1A, _2__1B, _3__2A, _4__2B, _5__2C, _6__2Y, _7__GND, _14__Vcc, _13__1C, _12__1Y, _11__3C, _10__3B, _9__3A, _8__3Y
  _7451 u_7451_1 ();  // open: _1__1A, _2__2A, _3__2B, _4__2C, _5__2D, _6__2Y, _7__GND, _14__Vcc, _13__1B, _12__NC, _11__NC, _10__1D, _9__1C, _8__1Y
  _74138 u_74138_1 ();  // open: _1__A, _2__B, _3__C, _4__G2A, _5__G2B, _6__G1, _7__Y7, _8__GND, _16__Vcc, _15__Y0, _14__Y1, _13__Y2, _12__Y3, _11__Y4, _10__Y5, _9__Y6
  _74154 u_74154_1 ();  // open: _1__Y0, _2__Y1, _3__Y2, _4__Y3, _5__Y4, _6__Y5, _7__Y6, _8__Y7, _9__Y8, _10__Y9, _11__Y10, _12__GND, _24__Vcc, _23__A, _22__B, _21__C, _20__D, _19__G2, _18__G1, _17__Y15, _16__Y14, _15__Y13, _14__Y12, _13__Y11
  _7411 u_7411_1 ();  // open: _1__1A, _2__1B, _3__2A, _4__2B, _5__2C, _6__2Y, _7__GND, _14__Vcc, _13__1C, _12__1Y, _11__3C, _10__3B, _9__3A, _8__3Y
  _74139 u_74139_1 ();  // open: _1__1G, _2__1A, _3__1B, _4__1Y0, _5__1Y1, _6__1Y2, _7__1Y3, _8__GND, _16__Vcc, _15__2G, _14__2A, _13__2B, _12__2Y0, _11__2Y1, _10__2Y2, _9__2Y3
  _74157 u_74157_1 ();  // open: _1__S, _2__A1, _3__B1, _4__Y1, _5__A2, _6__B2, _7__Y2, _8__GND, _16__Vcc, _15__G, _14__A4, _13__B4, _12__Y4, _11__A3, _10__B3, _9__Y3
  _74260 u_74260_1 ();  // open: _1__1A, _2__1B, _3__1E, _4__1C, _5__1D, _6__1Y, _7__GND, _14__Vcc, _13__2D, _12__2C, _11__2E, _10__2B, _9__2A, _8__2Y
  _7474 u_7474_1 ();  // open: _1__CLR1, _2__D1, _3__CLK1, _4__PR1, _5__Q1, _6__nQ1, _7__GND, _14__Vcc, _13__CLR2, _12__D2, _11__CLK2, _10__PR2, _9__Q2, _8__nQ2
  _74161 u_74161_1 ();  // open: _1__nMR, _2__CP, _3__D0, _4__D1, _5__D2, _6__D3, _7__CEP, _8__GND, _16__Vcc, _15__TC, _14__Q0, _13__Q1, _12__Q2, _11__O3, _10__CET, _9__nPE
  _74371 u_74371_1 ();  // open: _1__AD_A, _2__AD_B, _3__AD_C, _4__AD_D, _5__AD_E, _6__DO_1, _7__DO_2, _8__DO_3, _9__DO_4, _10__GND, _20__Vcc, _19__AD_H, _18__AD_G, _17__AD_F, _16__nS_2, _15__nS_1, _14__DO_8, _13__DO_7, _12__DO_6, _11__DO_5
  _7420 u_7420_1 ();  // open: _1__1A, _2__1B, _3__NC, _4__1C, _5__1D, _6__1Y, _7__GND, _14__Vcc, _13__2D, _12__2C, _11__NC, _10__2B, _9__2A, _8__2Y
  _7476 u_7476_1 ();  // open: _1__CLK1, _2__PR1, _3__CLR1, _4__J1, _5__VCC, _6__CLK2, _7__PR2, _8__CLR2, _16__K1, _15__Q1, _14__nQ1, _13__GND, _12__K2, _11__Q2, _10__nQ2, _9__J2
  _74147 u_74147_1 ();  // open: _1__I4, _2__I5, _3__I6, _4__I7, _5__I8, _6__A2, _7__A1, _8__GND, _16__Vcc, _15__NC, _14__A3, _13__I3, _12__I2, _11__I1, _10__I9, _9__A0
  _74163 u_74163_1 ();  // open: _1__nMR, _2__CP, _3__D0, _4__D1, _5__D2, _6__D3, _7__CEP, _8__GND, _16__Vcc, _15__TC, _14__Q0, _13__Q1, _12__Q2, _11__O3, _10__CET, _9__nPE
  _7421 u_7421_1 ();  // open: _1__1A, _2__1B, _3__NC, _4__1C, _5__1D, _6__1Y, _7__GND, _14__Vcc, _13__2D, _12__2C, _11__NC, _10__2B, _9__2A, _8__2Y
  _7483 u_7483_1 ();  // open: _1__A4, _2__S3, _3__A3, _4__B3, _5__Vcc, _6__S2, _7__B2, _8__A2, _16__B4, _15__S4, _14__Cout, _13__Cin, _12__GND, _11__B1, _10__A1, _9__S1
  _74148 u_74148_1 ();  // open: _1__I4, _2__I5, _3__I6, _4__I7, _5__nEI__NC, _6__A2, _7__A1, _8__GND, _16__Vcc, _15__nEO__NC, _14__nGS__NC, _13__I3, _12__I2, _11__I1, _10__I0, _9__A0
  _74682 u_74682_1 ();  // open: _1__A___B, _2__A0, _3__B0, _4__A1, _5__B1, _6__A2, _7__B2, _8__A3, _9__B3, _10__GND, _20__Vcc, _19__A___B, _18__B7, _17__A7, _16__B6, _15__A6, _14__B5, _13__A5, _12__B4, _11__A4

  // Notes on the sheet:
  //   Ben Oztalay, 2010
  //   benoztalay.wordpress.com
  //   This collection excludes duplicate integrated circuits, such as the 7401, since it has the same function as the 7400, it just has open-collector outputs
  //   quad 2-input
  //   NAND
  //   dual 4-input
  //   NOR
  //   quad 2-input
  //   XOR
  //   16 to 1 MUX
  //   hex D-type flip-flop
  //   with reset; positive-edge
  //   triple 3-input
  //   OR
  //   This is obviously an incomplete collection, although I believe it covers many applications. Feel free to add to it, I just ask that you follow the same
  //   conventions I've used and give credit where credit is due. Thanks!
  //   This is a library of 7400 series integrated circuits
  //   quad 2-input
  //   NOR
  //   triple 3-input
  //   NOR
  //   64-bit RAM
  //   8-bit bidirectional
  //   universal shift register
  //   hex inverter
  //   8-input NAND
  //   dual 4-bit latches
  //   8 to 1 MUX
  //   hex buffer
  //   quad 2-input
  //   dual 4 to 1 MUX
  //   3-to-8 line
  //   decoder/demultiplexer
  //   Pin placement reflects the arrangement of the actual integrated circuits, and power and ground pins are just dummy pins
  //   quad 2-input
  //   BCD to 7-segment
  //   OR
  //   13-input NAND
  //   4 to 16 decoder
  //   dual 4 to 1 MUX
  //   triple 3-input
  //   AND
  //   decoder
  //   3 to 8 decoder
  //   NAND
  //   dual 2-wide
  //   2-input AOI
  //   quad 2 to 1
  //   MUX
  //   dual 5-input
  //   NOR
  //   triple 3-input
  //   AND
  //   dual D
  //   flip-flop
  //   dual 2 to 4 
  //   decoder
  //   sync. 4-bit
  //   binary counter
  //   w/ async. clear
  //   256x8 ROM
  //   dual 4-input
  //   NAND
  //   dual JK
  //   flip-flop
  //   10 to 4 priority
  //   encoder
  //   sync. 4-bit
  //   binary counter
  //   w/ sync. clear
  //   8-bit magnitude
  //   dual 4-input
  //   AND
  //   4-bit binary
  //   full adder
  //   8 to 3 priority
  //   encoder
  //   comparator
endmodule

module _7400 (
  input  _1__1A,
  input  _14__Vcc,
  input  _2__1B,
  input  _13__4B,
  input  _12__4A,
  input  _4__2A,
  input  _5__2B,
  input  _10__3B,
  input  _9__3A,
  input  _7__GND,
  output _3__1Y,
  output _11__4Y,
  output _6__2Y,
  output _8__3Y
);

  nand nand_1 (_3__1Y, _2__1B, _1__1A);
  nand nand_2 (_6__2Y, _5__2B, _4__2A);
  nand nand_3 (_11__4Y, _13__4B, _12__4A);
  nand nand_4 (_8__3Y, _10__3B, _9__3A);

  // Notes on the sheet:
  //   7400: quad NAND
endmodule

module _7402 (
  input  _14__Vcc,
  input  _2__1A,
  input  _3__1B,
  input  _12__4B,
  input  _11__4A,
  input  _5__2A,
  input  _6__2B,
  input  _9__3B,
  input  _7__GND,
  input  _8__3A,
  output _1__1Y,
  output _13__4Y,
  output _4__2Y,
  output _10__3Y
);

  nor nor_1 (_1__1Y, _2__1A, _3__1B);
  nor nor_2 (_4__2Y, _5__2A, _6__2B);
  nor nor_3 (_13__4Y, _11__4A, _12__4B);
  nor nor_4 (_10__3Y, _8__3A, _9__3B);

  // Notes on the sheet:
  //   7402: quad NOR
endmodule

module _7404 (
  input  _1__1A,
  input  _14__Vcc,
  input  _13__6A,
  input  _3__2A,
  input  _11__5A,
  input  _5__3A,
  input  _9__4A,
  input  _7__GND,
  output _2__1Y,
  output _12__6Y,
  output _4__2Y,
  output _10__5Y,
  output _6__3Y,
  output _8__4Y
);

  not not_1 (_2__1Y, _1__1A);
  not not_2 (_4__2Y, _3__2A);
  not not_3 (_6__3Y, _5__3A);
  not not_4 (_12__6Y, _13__6A);
  not not_5 (_10__5Y, _11__5A);
  not not_6 (_8__4Y, _9__4A);

  // Notes on the sheet:
  //   7407: hex inverter
endmodule

module _7407 (
  input  _1__1A,
  input  _14__Vcc,
  input  _13__6A,
  input  _3__2A,
  input  _11__5A,
  input  _5__3A,
  input  _9__4A,
  input  _7__GND,
  output _2__1Y,
  output _12__6Y,
  output _4__2Y,
  output _10__5Y,
  output _6__3Y,
  output _8__4Y
);

  buf buffer_1 (_2__1Y, _1__1A);
  buf buffer_2 (_4__2Y, _3__2A);
  buf buffer_3 (_6__3Y, _5__3A);
  buf buffer_4 (_12__6Y, _13__6A);
  buf buffer_5 (_10__5Y, _11__5A);
  buf buffer_6 (_8__4Y, _9__4A);

  // Notes on the sheet:
  //   7407: hex buffer
endmodule

module _7408 (
  input  _1__1A,
  input  _14__Vcc,
  input  _2__1B,
  input  _13__4B,
  input  _12__4A,
  input  _4__2A,
  input  _5__2B,
  input  _10__3B,
  input  _9__3A,
  input  _7__GND,
  output _3__1Y,
  output _11__4Y,
  output _6__2Y,
  output _8__3Y
);

  and and_1 (_3__1Y, _2__1B, _1__1A);
  and and_2 (_6__2Y, _5__2B, _4__2A);
  and and_3 (_11__4Y, _13__4B, _12__4A);
  and and_4 (_8__3Y, _10__3B, _9__3A);

  // Notes on the sheet:
  //   7408: quad AND
endmodule

module _7410 (
  input  _1__1A,
  input  _14__Vcc,
  input  _2__1B,
  input  _13__1C,
  input  _3__2A,
  input  _4__2B,
  input  _11__3C,
  input  _5__2C,
  input  _10__3B,
  input  _9__3A,
  input  _7__GND,
  output _12__1Y,
  output _6__2Y,
  output _8__3Y
);

  nand nand_1 (_6__2Y, _5__2C, _4__2B, _3__2A);
  nand nand_2 (_12__1Y, _2__1B, _1__1A, _13__1C);
  nand nand_3 (_8__3Y, _11__3C, _10__3B, _9__3A);

  // Notes on the sheet:
  //   7410: triple 3-input NAND 
endmodule

module _7411 (
  input  _1__1A,
  input  _14__Vcc,
  input  _2__1B,
  input  _13__1C,
  input  _3__2A,
  input  _4__2B,
  input  _11__3C,
  input  _5__2C,
  input  _10__3B,
  input  _9__3A,
  input  _7__GND,
  output _12__1Y,
  output _6__2Y,
  output _8__3Y
);

  and and_1 (_6__2Y, _5__2C, _3__2A);
  and and_2 (_12__1Y, _2__1B, _13__1C);
  and and_3 (_8__3Y, _11__3C, _9__3A);

  // Notes on the sheet:
  //   7411: triple 3-input AND 
endmodule

module _7420 (
  input  _1__1A,
  input  _14__Vcc,
  input  _2__1B,
  input  _13__2D,
  input  _3__NC,
  input  _12__2C,
  input  _4__1C,
  input  _11__NC,
  input  _5__1D,
  input  _10__2B,
  input  _9__2A,
  input  _7__GND,
  output _6__1Y,
  output _8__2Y
);

  nand nand_1 (_6__1Y, _5__1D, _4__1C, _2__1B, _1__1A);
  nand nand_2 (_8__2Y, _13__2D, _12__2C, _10__2B, _9__2A);

  // Notes on the sheet:
  //   7420: dual 4-input NAND
endmodule

module _7421 (
  input  _1__1A,
  input  _14__Vcc,
  input  _2__1B,
  input  _13__2D,
  input  _3__NC,
  input  _12__2C,
  input  _4__1C,
  input  _11__NC,
  input  _5__1D,
  input  _10__2B,
  input  _9__2A,
  input  _7__GND,
  output _6__1Y,
  output _8__2Y
);

  and and_1 (_6__1Y, _5__1D, _4__1C, _2__1B, _1__1A);
  and and_2 (_8__2Y, _13__2D, _12__2C, _10__2B, _9__2A);

  // Notes on the sheet:
  //   7421: dual 4-input AND
endmodule

module _7425 (
  input  _1__1A,
  input  _14__Vcc,
  input  _2__1B,
  input  _13__2D,
  input  _3__NC,
  input  _12__2C,
  input  _4__1C,
  input  _11__NC,
  input  _5__1D,
  input  _10__2B,
  input  _9__2A,
  input  _7__GND,
  output _6__1Y,
  output _8__2Y
);

  nor nor_1 (_6__1Y, _5__1D, _4__1C, _2__1B, _1__1A);
  nor nor_2 (_8__2Y, _13__2D, _12__2C, _10__2B, _9__2A);

  // Notes on the sheet:
  //   7425: dual 4-input NOR
endmodule

module _7427 (
  input  _1__1A,
  input  _14__Vcc,
  input  _2__1B,
  input  _13__1C,
  input  _3__2A,
  input  _4__2B,
  input  _11__3C,
  input  _5__2C,
  input  _10__3B,
  input  _9__3A,
  input  _7__GND,
  output _12__1Y,
  output _6__2Y,
  output _8__3Y
);

  nor nor_1 (_6__2Y, _5__2C, _4__2B, _3__2A);
  nor nor_2 (_12__1Y, _2__1B, _1__1A, _13__1C);
  nor nor_3 (_8__3Y, _11__3C, _10__3B, _9__3A);

  // Notes on the sheet:
  //   7427: triple 3-input NOR 
endmodule

module _7430 (
  input  _1__1A,
  input  _14__Vcc,
  input  _2__1B,
  input  _13__NC,
  input  _3__1C,
  input  _12__1H,
  input  _4__1D,
  input  _11__1G,
  input  _5__1E,
  input  _10__NC,
  input  _6__1F,
  input  _9__NC,
  input  _7__GND,
  output _8__3Y
);

  nand nand_1 (_8__3Y, _6__1F, _5__1E, _4__1D, _3__1C, _2__1B, _1__1A, _12__1H, _11__1G);

  // Notes on the sheet:
  //   7430: 8-input NAND 
endmodule

module _7432 (
  input  _1__1A,
  input  _14__Vcc,
  input  _2__1B,
  input  _13__4B,
  input  _12__4A,
  input  _4__2A,
  input  _5__2B,
  input  _10__3B,
  input  _9__3A,
  input  _7__GND,
  output _3__1Y,
  output _11__4Y,
  output _6__2Y,
  output _8__3Y
);

  or or_1 (_3__1Y, _2__1B, _1__1A);
  or or_2 (_6__2Y, _5__2B, _4__2A);
  or or_3 (_11__4Y, _13__4B, _12__4A);
  or or_4 (_8__3Y, _10__3B, _9__3A);

  // Notes on the sheet:
  //   7432: quad OR
endmodule

module _7448 (
  input  _1__B,
  input  _16__Vcc,
  input  _2__C,
  input  _3__nLT,
  input  _4__NC,
  input  _5__nRBI,
  input  _6__D,
  input  _7__A,
  input  _8__GND,
  output _15__f,
  output _14__g,
  output _13__a,
  output _12__b,
  output _11__c,
  output _10__d,
  output _9__e
);

  wire nand_1_out, nand_2_out, nand_3_out, nand_4_out, nand_5_out, nand_6_out, nand_7_out, nand_8_out,
       nand_9_out, nand_10_out, nand_11_out, nand_12_out, nand_13_out, nand_14_out, nand_15_out, nand_16_out,
       nand_17_out, nand_18_out, nand_19_out, nand_20_out, nand_21_out, nand_22_out, nand_23_out,
       nand_24_out, nand_25_out, not_1_out, not_2_out, not_3_out;

  nand nand_1 (nand_1_out, _7__A, _3__nLT);
  nand nand_2 (nand_2_out, _1__B, _3__nLT);
  nand nand_3 (nand_3_out, _2__C, _3__nLT);
  not not_1 (not_1_out, _6__D);
  not not_2 (not_2_out, _5__nRBI);
  nand nand_4 (nand_4_out, nand_1_out, nand_8_out);
  nand nand_5 (nand_5_out, nand_2_out, nand_8_out);
  nand nand_6 (nand_6_out, nand_3_out, nand_8_out);
  nand nand_7 (nand_7_out, not_1_out, nand_8_out);
  nand nand_8 (nand_8_out, _3__nLT, not_2_out, not_1_out, nand_3_out, nand_2_out, nand_1_out);
  nand nand_9 (nand_9_out, nand_5_out, nand_7_out);
  nand nand_10 (nand_10_out, nand_1_out, nand_6_out);
  nand nand_11 (nand_11_out, nand_4_out, nand_2_out, nand_3_out, not_1_out);
  nand nand_12 (nand_12_out, nand_5_out, nand_7_out);
  nand nand_13 (nand_13_out, nand_4_out, nand_2_out, nand_6_out);
  nand nand_14 (nand_14_out, nand_1_out, nand_5_out, nand_6_out);
  nand nand_15 (nand_15_out, nand_6_out, nand_7_out);
  nand nand_16 (nand_16_out, nand_1_out, nand_5_out, nand_3_out);
  nand nand_17 (nand_17_out, nand_4_out, nand_2_out, nand_3_out);
  nand nand_18 (nand_18_out, nand_1_out, nand_2_out, nand_6_out);
  nand nand_19 (nand_19_out, nand_4_out, nand_5_out, nand_6_out);
  not not_3 (not_3_out, nand_4_out);
  nand nand_20 (nand_20_out, nand_2_out, nand_6_out);
  nand nand_21 (nand_21_out, nand_4_out, nand_5_out);
  nand nand_22 (nand_22_out, nand_5_out, nand_3_out);
  nand nand_23 (nand_23_out, nand_4_out, nand_3_out, not_1_out);
  nand nand_24 (nand_24_out, nand_4_out, nand_5_out, nand_6_out);
  nand nand_25 (nand_25_out, nand_2_out, nand_3_out, not_1_out, _3__nLT);
  and and_1 (_13__a, nand_9_out, nand_10_out, nand_11_out);
  and and_2 (_12__b, nand_12_out, nand_13_out, nand_14_out);
  and and_3 (_11__c, nand_15_out, nand_16_out);
  and and_4 (_10__d, nand_17_out, nand_18_out, nand_19_out);
  and and_5 (_9__e, not_3_out, nand_20_out);
  and and_6 (_15__f, nand_21_out, nand_22_out, nand_23_out);
  and and_7 (_14__g, nand_24_out, nand_25_out);

  // Notes on the sheet:
  //   7448: BCD to 7-segment decoder
endmodule

module _7451 (
  input  _1__1A,
  input  _14__Vcc,
  input  _2__2A,
  input  _13__1B,
  input  _3__2B,
  input  _12__NC,
  input  _4__2C,
  input  _11__NC,
  input  _5__2D,
  input  _10__1D,
  input  _9__1C,
  input  _7__GND,
  output _6__2Y,
  output _8__1Y
);

  wire and_1_out, and_2_out, and_3_out, and_4_out;

  nor nor_1 (_8__1Y, and_3_out, and_4_out);
  and and_1 (and_1_out, _2__2A, _3__2B);
  and and_2 (and_2_out, _4__2C, _5__2D);
  and and_3 (and_3_out, _1__1A, _13__1B);
  and and_4 (and_4_out, _10__1D, _9__1C);
  nor nor_2 (_6__2Y, and_2_out, and_1_out);

  // Notes on the sheet:
  //   7451: dual 2-wide 2-input AND-OR-Invert gate
endmodule

module _7474 (
  input  _1__CLR1,
  input  _14__Vcc,
  input  _2__D1,
  input  _13__CLR2,
  input  _3__CLK1,
  input  _12__D2,
  input  _4__PR1,
  input  _11__CLK2,
  input  _10__PR2,
  input  _7__GND,
  output _5__Q1,
  output _6__nQ1,
  output _9__Q2,
  output _8__nQ2
);

  D_Flip_Flop_part d_ff_1 (
    .clk(_3__CLK1), .D(_2__D1), .Q(_5__Q1), .Qn(_6__nQ1), .preset(_4__PR1), .reset(_1__CLR1));  // open: en
  D_Flip_Flop_part d_ff_2 (
    .clk(_11__CLK2), .D(_12__D2), .Q(_9__Q2), .Qn(_8__nQ2), .preset(_10__PR2), .reset(_13__CLR2));  // open: en

  // Notes on the sheet:
  //   7474: dual D-type flip flop
endmodule

module _7476 (
  input  _1__CLK1,
  input  _16__K1,
  input  _2__PR1,
  input  _3__CLR1,
  input  _4__J1,
  input  _13__GND,
  input  _5__VCC,
  input  _12__K2,
  input  _6__CLK2,
  input  _7__PR2,
  input  _8__CLR2,
  input  _9__J2,
  output _15__Q1,
  output _14__nQ1,
  output _11__Q2,
  output _10__nQ2
);

  J_K_Flip_Flop j_k_ff_1 (
    .J(_4__J1), .clk(_1__CLK1), .K(_16__K1), .Q(_15__Q1), .Qn(_14__nQ1), .preset(_2__PR1), .reset(_3__CLR1));  // open: en
  J_K_Flip_Flop j_k_ff_2 (
    .J(_9__J2), .clk(_6__CLK2), .K(_12__K2), .Q(_11__Q2), .Qn(_10__nQ2), .preset(_7__PR2), .reset(_8__CLR2));  // open: en

  // Notes on the sheet:
  //   7476: dual JK-type flip flop
endmodule

module _7483 (
  input  _1__A4,
  input  _16__B4,
  input  _3__A3,
  input  _14__Cout,
  input  _4__B3,
  input  _13__Cin,
  input  _5__Vcc,
  input  _12__GND,
  input  _11__B1,
  input  _7__B2,
  input  _10__A1,
  input  _8__A2,
  output _2__S3,
  output _15__S4,
  output _6__S2,
  output _9__S1
);

  wire and_1_out, and_2_out, and_3_out, and_4_out, and_5_out, and_6_out, and_7_out, and_8_out, and_9_out,
       and_10_out, and_11_out, and_12_out, and_13_out, and_14_out, nand_1_out, nand_2_out, nand_3_out,
       nand_4_out, nor_1_out, nor_2_out, nor_3_out, nor_4_out, nor_6_out, nor_7_out, nor_8_out, not_1_out,
       not_2_out, not_3_out, not_4_out, not_5_out, not_6_out;

  nand nand_1 (nand_1_out, _16__B4, _1__A4);
  nor nor_1 (nor_1_out, _16__B4, _1__A4);
  nand nand_2 (nand_2_out, _4__B3, _3__A3);
  nor nor_2 (nor_2_out, _4__B3, _3__A3);
  nand nand_3 (nand_3_out, _7__B2, _8__A2);
  nor nor_3 (nor_3_out, _7__B2, _8__A2);
  nand nand_4 (nand_4_out, _11__B1, _10__A1);
  nor nor_4 (nor_4_out, _11__B1, _10__A1);
  and and_1 (and_1_out, nor_2_out, nand_1_out);
  and and_2 (and_2_out, nor_3_out, nand_1_out, nand_2_out);
  and and_3 (and_3_out, nor_4_out, nand_1_out, nand_2_out, nand_3_out);
  and and_4 (and_4_out, nand_1_out, nand_2_out, nand_3_out, nand_4_out, not_2_out);
  not not_1 (not_1_out, nor_1_out);
  and and_5 (and_5_out, nor_3_out, nand_2_out);
  and and_6 (and_6_out, nor_4_out, nand_2_out, nand_3_out);
  and and_7 (and_7_out, nand_2_out, nand_3_out, nand_4_out, not_2_out);
  not not_2 (not_2_out, _13__Cin);
  not not_3 (not_3_out, nor_2_out);
  and and_8 (and_8_out, nor_4_out, nand_3_out);
  and and_9 (and_9_out, nand_3_out, nand_4_out, not_2_out);
  not not_4 (not_4_out, nor_3_out);
  and and_10 (and_10_out, nand_4_out, not_2_out);
  not not_5 (not_5_out, nor_4_out);
  not not_6 (not_6_out, not_2_out);
  nor nor_5 (_14__Cout, nor_1_out, and_1_out, and_2_out, and_3_out, and_4_out);
  and and_11 (and_11_out, nand_1_out, not_1_out);
  and and_12 (and_12_out, nand_2_out, not_3_out);
  and and_13 (and_13_out, nand_3_out, not_4_out);
  and and_14 (and_14_out, nand_4_out, not_5_out);
  xor xor_1 (_15__S4, and_11_out, nor_6_out);
  nor nor_6 (nor_6_out, nor_2_out, and_5_out, and_6_out, and_7_out);
  xor xor_2 (_2__S3, and_12_out, nor_7_out);
  nor nor_7 (nor_7_out, nor_3_out, and_8_out, and_9_out);
  xor xor_3 (_6__S2, and_13_out, nor_8_out);
  nor nor_8 (nor_8_out, nor_4_out, and_10_out);
  xor xor_4 (_9__S1, and_14_out, not_6_out);

  // Notes on the sheet:
  //   7483: 4-bit full adder
endmodule

module _7486 (
  input  _1__1A,
  input  _14__Vcc,
  input  _2__1B,
  input  _13__4B,
  input  _12__4A,
  input  _4__2A,
  input  _5__2B,
  input  _10__3B,
  input  _9__3A,
  input  _7__GND,
  output _3__1Y,
  output _11__4Y,
  output _6__2Y,
  output _8__3Y
);

  xor xor_1 (_3__1Y, _2__1B, _1__1A);
  xor xor_2 (_6__2Y, _5__2B, _4__2A);
  xor xor_3 (_11__4Y, _13__4B, _12__4A);
  xor xor_4 (_8__3Y, _10__3B, _9__3A);

  // Notes on the sheet:
  //   7486: quad XOR
endmodule

module _7489 (
  input  _1__A0,
  input  _16__Vcc,
  input  _2__nCS,
  input  _15__A1,
  input  _3__nWE,
  input  _14__A2,
  input  _4__D1,
  input  _13__A3,
  input  _12__D4,
  input  _6__D2,
  input  _10__D3,
  input  _8__GND,
  output _5__nO1,
  output _11__nO4,
  output _7__nO2,
  output _9__nO3
);

  wire not_1_out, not_2_out, or_1_out;
  wire [3:0] ram_1_data;

  not not_1 (not_1_out, _2__nCS);
  not not_2 (not_2_out, _3__nWE);
  or or_1 (or_1_out, not_2_out, not_1_out);
  RAM #(.addrWidth(4), .dataWidth(4), .bus("separate")) ram_1 (
    .addr({_13__A3, _14__A2, _15__A1, _1__A0}), .din({_12__D4, _10__D3, _6__D2, _4__D1}), .data(ram_1_data),
    .sel(not_1_out), .clk(not_2_out), .ld(or_1_out));  // open: str, clr
  assign {_11__nO4, _9__nO3, _7__nO2, _5__nO1} = ~ram_1_data;  // NOT_Gate not_3, 4 bits wide

  // Notes on the sheet:
  //   7489: 64-bit RAM
endmodule

module _74116 (
  input  _1__nMRa,
  input  _24__Vcc,
  input  _2__nE0a,
  input  _3__nE1a,
  input  _22__D3b,
  input  _4__D0a,
  input  _20__D2b,
  input  _6__D1a,
  input  _18__D1b,
  input  _8__D2a,
  input  _16__D0b,
  input  _10__D3a,
  input  _15__nE1b,
  input  _14__nE0b,
  input  _12__GND,
  input  _13__nMRb,
  output _23__Q3b,
  output _21__Q2b,
  output _5__Q0a,
  output _19__Q1b,
  output _7__Q1a,
  output _17__Q0b,
  output _9__Q2a,
  output _11__Q3a
);

  wire and_1_out, and_2_out, not_1_out, not_2_out;

  not not_1 (not_1_out, _1__nMRa);
  and and_1 (and_1_out, ~_2__nE0a, ~_3__nE1a);  // AND_Gate
  D_Flip_Flop_part #(.trigger("high")) d_ff_1 (
    .clk(and_1_out), .D(_4__D0a), .Q(_5__Q0a), .reset(not_1_out));  // open: Qn, preset, en
  D_Flip_Flop_part #(.trigger("high")) d_ff_2 (
    .clk(and_1_out), .D(_6__D1a), .Q(_7__Q1a), .reset(not_1_out));  // open: Qn, preset, en
  D_Flip_Flop_part #(.trigger("high")) d_ff_3 (
    .clk(and_1_out), .D(_8__D2a), .Q(_9__Q2a), .reset(not_1_out));  // open: Qn, preset, en
  D_Flip_Flop_part #(.trigger("high")) d_ff_4 (
    .clk(and_1_out), .D(_10__D3a), .Q(_11__Q3a), .reset(not_1_out));  // open: Qn, preset, en
  D_Flip_Flop_part #(.trigger("high")) d_ff_5 (
    .clk(and_2_out), .D(_22__D3b), .Q(_23__Q3b), .reset(not_2_out));  // open: Qn, preset, en
  D_Flip_Flop_part #(.trigger("high")) d_ff_6 (
    .clk(and_2_out), .D(_20__D2b), .Q(_21__Q2b), .reset(not_2_out));  // open: Qn, preset, en
  D_Flip_Flop_part #(.trigger("high")) d_ff_7 (
    .clk(and_2_out), .D(_18__D1b), .Q(_19__Q1b), .reset(not_2_out));  // open: Qn, preset, en
  D_Flip_Flop_part #(.trigger("high")) d_ff_8 (
    .clk(and_2_out), .D(_16__D0b), .Q(_17__Q0b), .reset(not_2_out));  // open: Qn, preset, en
  and and_2 (and_2_out, ~_15__nE1b, ~_14__nE0b);  // AND_Gate
  not not_2 (not_2_out, _13__nMRb);

  // Notes on the sheet:
  //   74116: dual 4-bit latches
endmodule

module _74133 (
  input  _1__A,
  input  _16__Vcc,
  input  _2__B,
  input  _15__M,
  input  _3__C,
  input  _14__L,
  input  _4__D,
  input  _13__K,
  input  _5__E,
  input  _12__J,
  input  _6__F,
  input  _11__I,
  input  _7__G,
  input  _10__H,
  input  _8__GND,
  output _9__Y
);

  nand nand_1 (_9__Y, _7__G, _6__F, _5__E, _4__D, _3__C, _2__B, _1__A, _15__M, _14__L, _13__K, _12__J, _11__I, _10__H);

  // Notes on the sheet:
  //   74133: 13-input NAND
endmodule

module _74138 (
  input  _1__A,
  input  _16__Vcc,
  input  _2__B,
  input  _3__C,
  input  _4__G2A,
  input  _5__G2B,
  input  _6__G1,
  input  _8__GND,
  output _15__Y0,
  output _14__Y1,
  output _13__Y2,
  output _12__Y3,
  output _11__Y4,
  output _7__Y7,
  output _10__Y5,
  output _9__Y6
);

  wire and_1_out, and_2_out, and_3_out, and_4_out, and_5_out, and_6_out, and_7_out, and_8_out, and_9_out,
       decoder_1_out0, decoder_1_out1, decoder_1_out2, decoder_1_out3, decoder_1_out4, decoder_1_out5,
       decoder_1_out6, decoder_1_out7, not_1_out, not_2_out;

  not not_1 (not_1_out, _4__G2A);
  not not_2 (not_2_out, _5__G2B);
  not not_3 (_7__Y7, and_1_out);
  and and_1 (and_1_out, and_2_out, decoder_1_out7);
  and and_2 (and_2_out, not_1_out, not_2_out, _6__G1);
  Decoder #(.select(3), .enable("false")) decoder_1 (
    .out0(decoder_1_out0), .out1(decoder_1_out1), .out2(decoder_1_out2), .out3(decoder_1_out3),
    .out4(decoder_1_out4), .out5(decoder_1_out5), .out6(decoder_1_out6), .out7(decoder_1_out7),
    .sel({_3__C, _2__B, _1__A}));
  and and_3 (and_3_out, and_2_out, decoder_1_out0);
  not not_4 (_15__Y0, and_3_out);
  not not_5 (_14__Y1, and_4_out);
  and and_4 (and_4_out, and_2_out, decoder_1_out1);
  and and_5 (and_5_out, and_2_out, decoder_1_out2);
  not not_6 (_13__Y2, and_5_out);
  and and_6 (and_6_out, and_2_out, decoder_1_out3);
  not not_7 (_12__Y3, and_6_out);
  not not_8 (_11__Y4, and_7_out);
  and and_7 (and_7_out, and_2_out, decoder_1_out4);
  and and_8 (and_8_out, and_2_out, decoder_1_out5);
  not not_9 (_10__Y5, and_8_out);
  and and_9 (and_9_out, and_2_out, decoder_1_out6);
  not not_10 (_9__Y6, and_9_out);

  // Notes on the sheet:
  //   74138: 3-Line to 8-Line Decoder
endmodule

module _74139 (
  input  _1__1G,
  input  _16__Vcc,
  input  _2__1A,
  input  _15__2G,
  input  _3__1B,
  input  _14__2A,
  input  _13__2B,
  input  _8__GND,
  output _4__1Y0,
  output _5__1Y1,
  output _12__2Y0,
  output _6__1Y2,
  output _11__2Y1,
  output _7__1Y3,
  output _10__2Y2,
  output _9__2Y3
);

  wire decoder_1_out0, decoder_1_out1, decoder_1_out2, decoder_1_out3, decoder_2_out0, decoder_2_out1,
       decoder_2_out2, decoder_2_out3, not_1_out, not_2_out, not_3_out, not_4_out, not_5_out, not_6_out,
       not_7_out, not_8_out, not_9_out, not_10_out;

  not not_1 (not_1_out, _1__1G);
  and and_1 (_4__1Y0, not_1_out, not_2_out);
  not not_2 (not_2_out, decoder_1_out0);
  and and_2 (_5__1Y1, not_1_out, not_3_out);
  not not_3 (not_3_out, decoder_1_out1);
  and and_3 (_6__1Y2, not_1_out, not_4_out);
  not not_4 (not_4_out, decoder_1_out2);
  and and_4 (_7__1Y3, not_1_out, not_5_out);
  not not_5 (not_5_out, decoder_1_out3);
  Decoder #(.select(2), .enable("false")) decoder_1 (
    .out0(decoder_1_out0), .out1(decoder_1_out1), .out2(decoder_1_out2), .out3(decoder_1_out3),
    .sel({_3__1B, _2__1A}));
  Decoder #(.select(2), .enable("false")) decoder_2 (
    .out0(decoder_2_out0), .out1(decoder_2_out1), .out2(decoder_2_out2), .out3(decoder_2_out3),
    .sel({_13__2B, _14__2A}));
  not not_6 (not_6_out, _15__2G);
  not not_7 (not_7_out, decoder_2_out0);
  not not_8 (not_8_out, decoder_2_out1);
  not not_9 (not_9_out, decoder_2_out2);
  not not_10 (not_10_out, decoder_2_out3);
  and and_5 (_12__2Y0, not_6_out, not_7_out);
  and and_6 (_11__2Y1, not_6_out, not_8_out);
  and and_7 (_10__2Y2, not_6_out, not_9_out);
  and and_8 (_9__2Y3, not_6_out, not_10_out);

  // Notes on the sheet:
  //   74139: Dual 2-Line to 4-Line Decoder
endmodule

module _74147 (
  input  _1__I4,
  input  _16__Vcc,
  input  _2__I5,
  input  _15__NC,
  input  _3__I6,
  input  _4__I7,
  input  _13__I3,
  input  _5__I8,
  input  _12__I2,
  input  _11__I1,
  input  _10__I9,
  input  _8__GND,
  output _14__A3,
  output _6__A2,
  output _7__A1,
  output _9__A0
);

  Priority_Encoder #(.select(4)) priority_encoder_1 (
    .in0(_11__I1), .in1(_12__I2), .in2(_13__I3), .in3(_1__I4), .in4(_2__I5), .in5(_3__I6), .in6(_4__I7),
    .in7(_5__I8), .in8(_10__I9), .out({_14__A3, _6__A2, _7__A1, _9__A0}));  // open: in9, in10, in11, in12, in13, in14, in15, gs, en_out, en_in

  // Notes on the sheet:
  //   74147: 9-Line to 4-Line Priority Encoder
endmodule

module _74148 (
  input  _1__I4,
  input  _16__Vcc,
  input  _2__I5,
  input  _15__nEO__NC,
  input  _3__I6,
  input  _14__nGS__NC,
  input  _4__I7,
  input  _13__I3,
  input  _5__nEI__NC,
  input  _12__I2,
  input  _6__A2,
  input  _11__I1,
  input  _7__A1,
  input  _10__I0,
  input  _8__GND,
  input  _9__A0
);

  Priority_Encoder priority_encoder_1 (
    .in0(_10__I0), .in1(_11__I1), .in2(_12__I2), .in3(_13__I3), .in4(_1__I4), .in5(_2__I5), .in6(_3__I6),
    .in7(_4__I7), .out({_7__A1, _6__A2, _9__A0}));  // open: en_in, gs, en_out

  // Notes on the sheet:
  //   74148: 9-Line to 4-Line Priority Encoder
  //   NOTE: Pins 5, 14, and 15 have connections normally, but I chose not to model them
endmodule

module _74150 (
  input  _1__E7,
  input  _24__Vcc,
  input  _2__E6,
  input  _23__E8,
  input  _3__E5,
  input  _22__E9,
  input  _4__E4,
  input  _21__E10,
  input  _5__E3,
  input  _20__E11,
  input  _6__E2,
  input  _19__E12,
  input  _7__E1,
  input  _18__E13,
  input  _8__E0,
  input  _17__E14,
  input  _9__nG,
  input  _16__E15,
  input  _15__A,
  input  _11__D,
  input  _14__B,
  input  _12__GND,
  input  _13__C,
  output _10__W
);

  wire multiplexer_1_out, not_1_out;

  or or_1 (_10__W, _9__nG, not_1_out);
  not not_1 (not_1_out, multiplexer_1_out);
  Multiplexer #(.select(4), .enable("false")) multiplexer_1 (
    .in0(_8__E0), .in1(_7__E1), .in2(_6__E2), .in3(_5__E3), .in4(_4__E4), .in5(_3__E5), .in6(_2__E6),
    .in7(_1__E7), .in8(_23__E8), .in9(_22__E9), .in10(_21__E10), .in11(_20__E11), .in12(_19__E12),
    .in13(_18__E13), .in14(_17__E14), .in15(_16__E15), .out(multiplexer_1_out),
    .sel({_11__D, _13__C, _14__B, _15__A}));

  // Notes on the sheet:
  //   74150: 16-Line to 1-Line Multiplexer
endmodule

module _74151 (
  input  _1__D3,
  input  _16__Vcc,
  input  _2__D2,
  input  _15__D4,
  input  _3__D1,
  input  _14__D5,
  input  _4__D0,
  input  _13__D6,
  input  _12__D7,
  input  _11__A,
  input  _7__nG,
  input  _10__B,
  input  _8__GND,
  input  _9__C,
  output _5__Y,
  output _6__W
);

  wire multiplexer_1_out, not_2_out;

  not not_1 (_5__Y, _6__W);
  or or_1 (_6__W, not_2_out, _7__nG);
  Multiplexer #(.select(3), .enable("false")) multiplexer_1 (
    .in0(_4__D0), .in1(_3__D1), .in2(_2__D2), .in3(_1__D3), .in4(_15__D4), .in5(_14__D5), .in6(_13__D6),
    .in7(_12__D7), .out(multiplexer_1_out), .sel({_9__C, _10__B, _11__A}));
  not not_2 (not_2_out, multiplexer_1_out);

  // Notes on the sheet:
  //   74151: 8-Line to 1-Line Multiplexer
endmodule

module _74153 (
  input  _1__nG1,
  input  _16__Vcc,
  input  _2__B,
  input  _15__nG2,
  input  _3__1C3,
  input  _14__A,
  input  _4__1C2,
  input  _13__2C3,
  input  _5__1C1,
  input  _12__2C2,
  input  _6__1C0,
  input  _11__2C1,
  input  _10__2C0,
  input  _8__GND,
  output _7__Y1,
  output _9__Y2
);

  wire multiplexer_1_out, multiplexer_2_out, not_1_out, not_2_out;

  not not_1 (not_1_out, _1__nG1);
  Multiplexer #(.select(2), .enable("false")) multiplexer_1 (
    .in0(_6__1C0), .in1(_5__1C1), .in2(_4__1C2), .in3(_3__1C3), .out(multiplexer_1_out), .sel({_2__B, _14__A}));
  and and_1 (_7__Y1, multiplexer_1_out, not_1_out);
  not not_2 (not_2_out, _15__nG2);
  Multiplexer #(.select(2), .enable("false")) multiplexer_2 (
    .in0(_10__2C0), .in1(_11__2C1), .in2(_12__2C2), .in3(_13__2C3), .out(multiplexer_2_out),
    .sel({_2__B, _14__A}));
  and and_2 (_9__Y2, multiplexer_2_out, not_2_out);

  // Notes on the sheet:
  //   74153: Dual 4-Line to 1-Line Multiplexer
endmodule

module _74154 (
  input  _24__Vcc,
  input  _23__A,
  input  _22__B,
  input  _21__C,
  input  _20__D,
  input  _19__G2,
  input  _18__G1,
  input  _12__GND,
  output _1__Y0,
  output _2__Y1,
  output _3__Y2,
  output _4__Y3,
  output _5__Y4,
  output _6__Y5,
  output _7__Y6,
  output _8__Y7,
  output _17__Y15,
  output _9__Y8,
  output _16__Y14,
  output _10__Y9,
  output _15__Y13,
  output _11__Y10,
  output _14__Y12,
  output _13__Y11
);

  wire and_12_out, decoder_1_out0, decoder_1_out1, decoder_1_out2, decoder_1_out3, decoder_1_out4,
       decoder_1_out5, decoder_1_out6, decoder_1_out7, decoder_1_out8, decoder_1_out9, decoder_1_out10,
       decoder_1_out11, decoder_1_out12, decoder_1_out13, decoder_1_out14, decoder_1_out15, not_1_out,
       not_2_out, not_3_out, not_4_out, not_5_out, not_6_out, not_7_out, not_8_out, not_9_out, not_10_out,
       not_11_out, not_12_out, not_13_out, not_14_out, not_15_out, not_16_out, not_17_out, not_18_out;

  not not_1 (not_1_out, decoder_1_out0);
  and and_1 (_1__Y0, not_1_out, and_12_out);
  not not_2 (not_2_out, decoder_1_out1);
  and and_2 (_2__Y1, not_2_out, and_12_out);
  not not_3 (not_3_out, decoder_1_out2);
  and and_3 (_3__Y2, not_3_out, and_12_out);
  not not_4 (not_4_out, decoder_1_out3);
  and and_4 (_4__Y3, not_4_out, and_12_out);
  not not_5 (not_5_out, decoder_1_out4);
  and and_5 (_5__Y4, not_5_out, and_12_out);
  not not_6 (not_6_out, decoder_1_out5);
  and and_6 (_6__Y5, not_6_out, and_12_out);
  not not_7 (not_7_out, decoder_1_out6);
  and and_7 (_7__Y6, not_7_out, and_12_out);
  not not_8 (not_8_out, decoder_1_out7);
  and and_8 (_8__Y7, not_8_out, and_12_out);
  not not_9 (not_9_out, decoder_1_out8);
  and and_9 (_9__Y8, not_9_out, and_12_out);
  not not_10 (not_10_out, decoder_1_out9);
  and and_10 (_10__Y9, not_10_out, and_12_out);
  not not_11 (not_11_out, decoder_1_out10);
  and and_11 (_11__Y10, not_11_out, and_12_out);
  and and_12 (and_12_out, not_12_out, not_13_out);
  Decoder #(.select(4), .enable("false")) decoder_1 (
    .out0(decoder_1_out0), .out1(decoder_1_out1), .out2(decoder_1_out2), .out3(decoder_1_out3),
    .out4(decoder_1_out4), .out5(decoder_1_out5), .out6(decoder_1_out6), .out7(decoder_1_out7),
    .out8(decoder_1_out8), .out9(decoder_1_out9), .out10(decoder_1_out10), .out11(decoder_1_out11),
    .out12(decoder_1_out12), .out13(decoder_1_out13), .out14(decoder_1_out14), .out15(decoder_1_out15),
    .sel({_20__D, _21__C, _22__B, _23__A}));
  not not_12 (not_12_out, _19__G2);
  not not_13 (not_13_out, _18__G1);
  not not_14 (not_14_out, decoder_1_out15);
  and and_13 (_17__Y15, not_14_out, and_12_out);
  not not_15 (not_15_out, decoder_1_out14);
  and and_14 (_16__Y14, not_15_out, and_12_out);
  not not_16 (not_16_out, decoder_1_out13);
  and and_15 (_15__Y13, not_16_out, and_12_out);
  not not_17 (not_17_out, decoder_1_out12);
  and and_16 (_14__Y12, not_17_out, and_12_out);
  not not_18 (not_18_out, decoder_1_out11);
  and and_17 (_13__Y11, not_18_out, and_12_out);

  // Notes on the sheet:
  //   74154: 4-Line to 16-Line Decoder
endmodule

module _74157 (
  input  _1__S,
  input  _16__Vcc,
  input  _2__A1,
  input  _15__G,
  input  _3__B1,
  input  _14__A4,
  input  _13__B4,
  input  _5__A2,
  input  _6__B2,
  input  _11__A3,
  input  _10__B3,
  input  _8__GND,
  output _4__Y1,
  output _12__Y4,
  output _7__Y2,
  output _9__Y3
);

  wire multiplexer_1_out, multiplexer_2_out, multiplexer_3_out, multiplexer_4_out, not_1_out;

  Multiplexer #(.enable("false")) multiplexer_1 (.in0(_2__A1), .in1(_3__B1), .out(multiplexer_1_out), .sel(_1__S));
  and and_1 (_4__Y1, multiplexer_1_out, not_1_out);
  Multiplexer #(.enable("false")) multiplexer_2 (.in0(_5__A2), .in1(_6__B2), .out(multiplexer_2_out), .sel(_1__S));
  and and_2 (_7__Y2, multiplexer_2_out, not_1_out);
  not not_1 (not_1_out, _15__G);
  Multiplexer #(.enable("false")) multiplexer_3 (.in0(_14__A4), .in1(_13__B4), .out(multiplexer_3_out), .sel(_1__S));
  and and_3 (_12__Y4, multiplexer_3_out, not_1_out);
  Multiplexer #(.enable("false")) multiplexer_4 (.in0(_11__A3), .in1(_10__B3), .out(multiplexer_4_out), .sel(_1__S));
  and and_4 (_9__Y3, multiplexer_4_out, not_1_out);

  // Notes on the sheet:
  //   74157: Quad 2-Line to 1-Line Multiplexer
endmodule

module _74161 (
  input  _1__nMR,
  input  _16__Vcc,
  input  _2__CP,
  input  _3__D0,
  input  _4__D1,
  input  _5__D2,
  input  _6__D3,
  input  _7__CEP,
  input  _10__CET,
  input  _8__GND,
  input  _9__nPE,
  output _15__TC,
  output _14__Q0,
  output _13__Q1,
  output _12__Q2,
  output _11__O3
);

  wire and_1_out, counter_1_carry, not_1_out, not_2_out;

  not not_1 (not_1_out, _1__nMR);
  and and_1 (and_1_out, _7__CEP, _9__nPE, _10__CET);
  Counter #(.width(4), .max('hf)) counter_1 (
    .load(not_2_out), .D({_6__D3, _5__D2, _4__D1, _3__D0}), .count(and_1_out),
    .Q({_11__O3, _12__Q2, _13__Q1, _14__Q0}), .carry(counter_1_carry), .clk(_2__CP), .clr(not_1_out));
  and and_2 (_15__TC, counter_1_carry, _10__CET);
  not not_2 (not_2_out, _9__nPE);

  // Notes on the sheet:
  //   74161: Synchronous 4-bit Binary Counter with Asynchronous Clear 
endmodule

module _74163 (
  input  _1__nMR,
  input  _16__Vcc,
  input  _2__CP,
  input  _3__D0,
  input  _4__D1,
  input  _5__D2,
  input  _6__D3,
  input  _7__CEP,
  input  _10__CET,
  input  _8__GND,
  input  _9__nPE,
  output _15__TC,
  output _14__Q0,
  output _13__Q1,
  output _12__Q2,
  output _11__O3
);

  wire and_1_out, and_2_out, counter_1_carry, not_1_out, not_2_out;
  wire [3:0] multiplexer_1_out;

  not not_1 (not_1_out, _1__nMR);
  Multiplexer #(.width(4), .enable("false")) multiplexer_1 (
    .in0({_6__D3, _5__D2, _4__D1, _3__D0}), .in1(4'b0000), .out(multiplexer_1_out), .sel(not_1_out));
  and and_1 (and_1_out, _7__CEP, and_2_out, _10__CET);
  not not_2 (not_2_out, and_2_out);
  Counter #(.width(4), .max('hf)) counter_1 (
    .load(not_2_out), .D(multiplexer_1_out), .count(and_1_out), .Q({_11__O3, _12__Q2, _13__Q1, _14__Q0}),
    .carry(counter_1_carry), .clk(_2__CP));  // open: clr
  and and_2 (and_2_out, ~not_1_out, _9__nPE);  // AND_Gate
  and and_3 (_15__TC, counter_1_carry, _10__CET);

  // Notes on the sheet:
  //   74163: Synchronous 4-bit Binary Counter with Synchronous Clear 
endmodule

module _74174 (
  input  _1__MR_prime,
  input  _16__Vcc,
  input  _3__D0,
  input  _14__D5,
  input  _4__D1,
  input  _13__D4,
  input  _6__D2,
  input  _11__D3,
  input  _8__GND,
  input  _9__CP,
  output _2__Q0,
  output _15__Q5,
  output _5__Q1,
  output _12__Q4,
  output _7__Q2,
  output _10__Q3
);

  wire not_1_out;

  not not_1 (not_1_out, _1__MR_prime);
  D_Flip_Flop_part #(.trigger("high")) d_ff_1 (
    .clk(_9__CP), .D(_3__D0), .Q(_2__Q0), .reset(not_1_out));  // open: Qn, preset, en
  D_Flip_Flop_part #(.trigger("high")) d_ff_2 (
    .clk(_9__CP), .D(_4__D1), .Q(_5__Q1), .reset(not_1_out));  // open: Qn, preset, en
  D_Flip_Flop_part #(.trigger("high")) d_ff_3 (
    .clk(_9__CP), .D(_6__D2), .Q(_7__Q2), .reset(not_1_out));  // open: Qn, preset, en
  D_Flip_Flop_part #(.trigger("high")) d_ff_4 (
    .clk(_9__CP), .D(_14__D5), .Q(_15__Q5), .reset(not_1_out));  // open: Qn, preset, en
  D_Flip_Flop_part #(.trigger("high")) d_ff_5 (
    .clk(_9__CP), .D(_13__D4), .Q(_12__Q4), .reset(not_1_out));  // open: Qn, preset, en
  D_Flip_Flop_part #(.trigger("high")) d_ff_6 (
    .clk(_9__CP), .D(_11__D3), .Q(_10__Q3), .reset(not_1_out));  // open: Qn, preset, en

  // Notes on the sheet:
  //   74174: Hex D-type flip-flop with reset; positive-edge trigger
endmodule

module _74198 (
  input  _1__S0,
  input  _24__Vcc,
  input  _2__Dsr,
  input  _23__S1,
  input  _3__P0,
  input  _22__Dsl,
  input  _21__P7,
  input  _5__P1,
  input  _19__P6,
  input  _7__P2,
  input  _17__P5,
  input  _9__P3,
  input  _15__P4,
  input  _11__CP,
  input  _12__GND,
  input  _13__nMR,
  output _4__Q0,
  output _20__Q7,
  output _6__Q1,
  output _18__Q6,
  output _8__Q2,
  output _16__Q5,
  output _10__Q3,
  output _14__Q4
);

  wire and_1_out, and_2_out, and_3_out, and_4_out, and_5_out, and_6_out, and_7_out, and_8_out, and_9_out,
       and_10_out, and_11_out, and_12_out, and_13_out, and_14_out, and_15_out, and_16_out, and_17_out,
       and_18_out, and_19_out, and_20_out, and_21_out, and_22_out, and_23_out, and_24_out, and_25_out,
       nor_1_out, not_1_out, not_2_out, not_3_out, or_1_out, or_2_out, or_3_out, or_4_out, or_5_out,
       or_6_out, or_7_out, or_8_out, or_9_out;

  not not_1 (not_1_out, _23__S1);
  not not_2 (not_2_out, _1__S0);
  nor nor_1 (nor_1_out, not_2_out, not_1_out);
  and and_1 (and_1_out, not_1_out, not_2_out);
  and and_2 (and_2_out, _22__Dsl, not_2_out);
  and and_3 (and_3_out, _21__P7, nor_1_out);
  and and_4 (and_4_out, _18__Q6, not_1_out);
  and and_5 (and_5_out, _20__Q7, not_2_out);
  and and_6 (and_6_out, _19__P6, nor_1_out);
  and and_7 (and_7_out, _16__Q5, not_1_out);
  and and_8 (and_8_out, _18__Q6, not_2_out);
  and and_9 (and_9_out, _17__P5, nor_1_out);
  and and_10 (and_10_out, _14__Q4, not_1_out);
  and and_11 (and_11_out, _16__Q5, not_2_out);
  and and_12 (and_12_out, _15__P4, nor_1_out);
  and and_13 (and_13_out, _10__Q3, not_1_out);
  and and_14 (and_14_out, _14__Q4, not_2_out);
  and and_15 (and_15_out, _9__P3, nor_1_out);
  and and_16 (and_16_out, _8__Q2, not_1_out);
  and and_17 (and_17_out, _10__Q3, not_2_out);
  and and_18 (and_18_out, _7__P2, nor_1_out);
  and and_19 (and_19_out, _6__Q1, not_1_out);
  and and_20 (and_20_out, _8__Q2, not_2_out);
  and and_21 (and_21_out, _5__P1, nor_1_out);
  and and_22 (and_22_out, _4__Q0, not_1_out);
  and and_23 (and_23_out, _6__Q1, not_2_out);
  and and_24 (and_24_out, _3__P0, nor_1_out);
  and and_25 (and_25_out, _2__Dsr, not_1_out);
  or or_1 (or_1_out, _11__CP, and_1_out);
  or or_2 (or_2_out, and_2_out, and_3_out, and_4_out);
  or or_3 (or_3_out, and_5_out, and_6_out, and_7_out);
  or or_4 (or_4_out, and_8_out, and_9_out, and_10_out);
  or or_5 (or_5_out, and_11_out, and_12_out, and_13_out);
  or or_6 (or_6_out, and_14_out, and_15_out, and_16_out);
  or or_7 (or_7_out, and_17_out, and_18_out, and_19_out);
  or or_8 (or_8_out, and_20_out, and_21_out, and_22_out);
  or or_9 (or_9_out, and_23_out, and_24_out, and_25_out);
  D_Flip_Flop_part d_ff_1 (.clk(or_1_out), .D(or_2_out), .Q(_20__Q7), .reset(not_3_out));  // open: Qn, preset, en
  D_Flip_Flop_part d_ff_2 (.clk(or_1_out), .D(or_3_out), .Q(_18__Q6), .reset(not_3_out));  // open: Qn, preset, en
  D_Flip_Flop_part d_ff_3 (.clk(or_1_out), .D(or_4_out), .Q(_16__Q5), .reset(not_3_out));  // open: Qn, preset, en
  D_Flip_Flop_part d_ff_4 (.clk(or_1_out), .D(or_5_out), .Q(_14__Q4), .reset(not_3_out));  // open: Qn, preset, en
  not not_3 (not_3_out, _13__nMR);
  D_Flip_Flop_part d_ff_5 (.clk(or_1_out), .D(or_6_out), .Q(_10__Q3), .reset(not_3_out));  // open: Qn, preset, en
  D_Flip_Flop_part d_ff_6 (.clk(or_1_out), .D(or_7_out), .Q(_8__Q2), .reset(not_3_out));  // open: Qn, preset, en
  D_Flip_Flop_part d_ff_7 (.clk(or_1_out), .D(or_8_out), .Q(_6__Q1), .reset(not_3_out));  // open: Qn, preset, en
  D_Flip_Flop_part d_ff_8 (.clk(or_1_out), .D(or_9_out), .Q(_4__Q0), .reset(not_3_out));  // open: Qn, preset, en

  // Notes on the sheet:
  //   74198: 8-bit universal shift register
endmodule

module _74238 (
  input  _1__A0,
  input  _16__Vcc,
  input  _2__A1,
  input  _3__A2,
  input  _4__E1_prime,
  input  _5__E2_prime,
  input  _6__E3,
  input  _8__GND,
  output _15__Y0,
  output _14__Y1,
  output _13__Y2,
  output _12__Y3,
  output _11__Y4,
  output _7__Y7,
  output _10__Y5,
  output _9__Y6
);

  wire and_1_out;

  and and_1 (and_1_out, ~_4__E1_prime, ~_5__E2_prime, _6__E3);  // AND_Gate
  Demultiplexer #(.select(3), .enable("false")) demultiplexer_1 (
    .out0(_15__Y0), .out1(_14__Y1), .out2(_13__Y2), .out3(_12__Y3), .out4(_11__Y4), .out5(_10__Y5),
    .out6(_9__Y6), .out7(_7__Y7), .in(and_1_out), .sel({_3__A2, _2__A1, _1__A0}));

  // Notes on the sheet:
  //   74238: 3-to-8 line decoder/demultiplexer; non-inverting
endmodule

module _74253 (
  input  _1__1G,
  input  _16__Vcc,
  input  _2__Sb,
  input  _15__2G,
  input  _3__1C3,
  input  _14__Sa,
  input  _4__1C2,
  input  _13__2C3,
  input  _5__1C1,
  input  _12__2C2,
  input  _6__1C0,
  input  _11__2C1,
  input  _10__2C0,
  input  _8__GND,
  output _7__1Y,
  output _9__2Y
);

  wire multiplexer_1_out, multiplexer_2_out, not_1_out, not_3_out;
  wire [1:0] not_4_out;

  not not_1 (not_1_out, _1__1G);
  not not_2 (not_4_out[1], _2__Sb);
  Multiplexer #(.select(2), .enable("false")) multiplexer_1 (
    .in0(_3__1C3), .in1(_4__1C2), .in2(_5__1C1), .in3(_6__1C0), .out(multiplexer_1_out), .sel(not_4_out));
  and and_1 (_7__1Y, multiplexer_1_out, not_1_out);
  Multiplexer #(.select(2), .enable("false")) multiplexer_2 (
    .in0(_13__2C3), .in1(_12__2C2), .in2(_11__2C1), .in3(_10__2C0), .out(multiplexer_2_out), .sel(not_4_out));
  not not_3 (not_3_out, _15__2G);
  not not_4 (not_4_out[0], _14__Sa);
  and and_2 (_9__2Y, multiplexer_2_out, not_3_out);

  // Notes on the sheet:
  //   74253: Dual 4-Lin to 1-Line Multiplexer
endmodule

module _74260 (
  input  _1__1A,
  input  _14__Vcc,
  input  _2__1B,
  input  _13__2D,
  input  _3__1E,
  input  _12__2C,
  input  _4__1C,
  input  _11__2E,
  input  _5__1D,
  input  _10__2B,
  input  _9__2A,
  input  _7__GND,
  output _6__1Y,
  output _8__2Y
);

  nor nor_1 (_6__1Y, _5__1D, _4__1C, _3__1E, _2__1B, _1__1A);
  nor nor_2 (_8__2Y, _13__2D, _12__2C, _11__2E, _10__2B, _9__2A);

  // Notes on the sheet:
  //   74260: dual 5-input NOR
endmodule

module _74371 (
  input  _1__AD_A,
  input  _20__Vcc,
  input  _2__AD_B,
  input  _19__AD_H,
  input  _3__AD_C,
  input  _18__AD_G,
  input  _4__AD_D,
  input  _17__AD_F,
  input  _5__AD_E,
  input  _16__nS_2,
  input  _6__DO_1,
  input  _15__nS_1,
  input  _7__DO_2,
  input  _14__DO_8,
  input  _8__DO_3,
  input  _13__DO_7,
  input  _9__DO_4,
  input  _12__DO_6,
  input  _10__GND,
  input  _11__DO_5
);

  wire or_1_out;

  or or_1 (or_1_out, _16__nS_2, _15__nS_1);
  ROM rom_1 (
    .addr({_19__AD_H, _18__AD_G, _17__AD_F, _5__AD_E, _4__AD_D, _3__AD_C, _2__AD_B, _1__AD_A}),
    .data({_14__DO_8, _13__DO_7, _12__DO_6, _11__DO_5, _9__DO_4, _8__DO_3, _7__DO_2, _6__DO_1}),
    .sel(or_1_out));

  // Notes on the sheet:
  //   74371: 2048-bit ROM, 256x8
endmodule

module _74682 (
  input  _20__Vcc,
  input  _2__A0,
  input  _3__B0,
  input  _18__B7,
  input  _4__A1,
  input  _17__A7,
  input  _5__B1,
  input  _16__B6,
  input  _6__A2,
  input  _15__A6,
  input  _7__B2,
  input  _14__B5,
  input  _8__A3,
  input  _13__A5,
  input  _9__B3,
  input  _12__B4,
  input  _10__GND,
  input  _11__A4,
  output _1__A___B,
  output _19__A___B
);

  wire and_1_out, and_2_out, and_3_out, and_4_out, and_5_out, and_6_out, and_7_out, and_8_out, not_1_out,
       not_2_out, not_3_out, not_4_out, not_5_out, not_6_out, not_7_out, not_8_out, not_9_out, not_10_out,
       not_11_out, not_12_out, not_13_out, not_14_out, not_15_out, not_16_out, not_17_out, not_18_out,
       not_19_out, not_20_out, not_21_out, not_22_out, not_23_out, not_24_out, xnor_1_out, xnor_3_out,
       xnor_4_out, xnor_5_out, xnor_6_out, xnor_8_out;

  not not_1 (not_1_out, _2__A0);
  not not_2 (not_2_out, _3__B0);
  not not_3 (not_3_out, _4__A1);
  not not_4 (not_4_out, _5__B1);
  not not_5 (not_5_out, _6__A2);
  not not_6 (not_6_out, _7__B2);
  not not_7 (not_7_out, _8__A3);
  not not_8 (not_8_out, _9__B3);
  not not_9 (not_9_out, _11__A4);
  not not_10 (not_10_out, _12__B4);
  not not_11 (not_11_out, _13__A5);
  not not_12 (not_12_out, _14__B5);
  not not_13 (not_13_out, _15__A6);
  not not_14 (not_14_out, _16__B6);
  not not_15 (not_15_out, _17__A7);
  not not_16 (not_16_out, _18__B7);
  xnor xnor_1 (xnor_1_out, not_1_out, not_2_out);
  xnor xnor_2 (not_16_out, not_3_out, not_4_out);
  xnor xnor_3 (xnor_3_out, not_5_out, not_6_out);
  xnor xnor_4 (xnor_4_out, not_7_out, not_8_out);
  xnor xnor_5 (xnor_5_out, not_9_out, not_10_out);
  xnor xnor_6 (xnor_6_out, not_11_out, not_12_out);
  xnor xnor_7 (xnor_4_out, not_13_out, not_14_out);
  xnor xnor_8 (xnor_8_out, not_15_out, not_16_out);
  not not_17 (not_17_out, not_15_out);
  not not_18 (not_18_out, not_13_out);
  not not_19 (not_19_out, not_11_out);
  not not_20 (not_20_out, not_9_out);
  not not_21 (not_21_out, not_7_out);
  not not_22 (not_22_out, not_5_out);
  not not_23 (not_23_out, not_3_out);
  not not_24 (not_24_out, not_1_out);
  and and_1 (and_1_out, xnor_1_out, not_16_out, xnor_3_out, xnor_4_out, xnor_5_out, xnor_6_out, xnor_4_out, not_16_out, not_17_out);
  and and_2 (and_2_out, xnor_1_out, not_16_out, xnor_3_out, xnor_4_out, xnor_5_out, xnor_6_out, not_14_out, not_18_out);
  and and_3 (and_3_out, xnor_1_out, not_16_out, xnor_3_out, xnor_4_out, xnor_5_out, not_12_out, not_19_out);
  and and_4 (and_4_out, xnor_1_out, not_16_out, xnor_3_out, xnor_4_out, not_10_out, not_20_out);
  and and_5 (and_5_out, xnor_1_out, not_16_out, xnor_3_out, not_8_out, not_21_out);
  and and_6 (and_6_out, xnor_1_out, not_16_out, not_6_out, not_22_out);
  and and_7 (and_7_out, xnor_1_out, not_4_out, not_23_out);
  and and_8 (and_8_out, not_2_out, not_24_out);
  nand nand_1 (_19__A___B, xnor_1_out, not_16_out, xnor_3_out, xnor_4_out, xnor_5_out, xnor_6_out, xnor_4_out, xnor_8_out);
  nor nor_1 (_1__A___B, and_1_out, and_2_out, and_3_out, and_4_out, and_5_out, and_6_out, and_7_out, and_8_out);

  // Notes on the sheet:
  //   74682: 8-bit magnitude comparator 
endmodule

module _744075 (
  input  _1__1A,
  input  _14__Vcc,
  input  _2__1B,
  input  _13__1C,
  input  _3__2A,
  input  _4__2B,
  input  _11__3C,
  input  _5__2C,
  input  _10__3B,
  input  _9__3A,
  input  _7__GND,
  output _12__1Y,
  output _6__2Y,
  output _8__3Y
);

  or or_1 (_6__2Y, _5__2C, _4__2B, _3__2A);
  or or_2 (_12__1Y, _2__1B, _1__1A, _13__1C);
  or or_3 (_8__3Y, _11__3C, _10__3B, _9__3A);

  // Notes on the sheet:
  //   744075: triple 3-input OR 
endmodule

module README (
);

  IC_7400 ic_7400_1 ();  // open: A1, B1, A2, B2, A3, B3, A4, B4, Y1, Y2, Y3, Y4
  IC_7414 ic_7414_1 ();  // open: A1, A2, A3, A4, A5, A6, Y1, Y2, Y3, Y4, Y5, Y6
  IC_7473 ic_7473_1 ();  // open: J1, CLK1, K1, CLR1, J2, CLK2, K2, CLR2, Q1, R1, Q2, R2
  IC_74109 ic_74109_1 ();  // open: SET1, J1, CLK1, K1, CLR1, SET2, J2, CLK2, K2, CLR2, Q1, R1, Q2, R2
  IC_74157 ic_74157_1 ();  // open: A1, B1, A2, B2, A3, B3, A4, B4, S0, OE, Y1, Y2, Y3, Y4
  IC_74374 ic_74374_1 ();  // open: D1, D2, D3, D4, D5, D6, D7, D8, CLK, OE, Y1, Y2, Y3, Y4, Y5, Y6, Y7, Y8
  IC_7402 ic_7402_1 ();  // open: A1, B1, A2, B2, A3, B3, A4, B4, Y1, Y2, Y3, Y4
  IC_7420 ic_7420_1 ();  // open: A1, A2, B1, B2, C1, C2, D1, D2, Y1, Y2
  IC_7474 ic_7474_1 ();  // open: SET1, D1, CLK1, CLR1, SET2, D2, CLK2, CLR2, Q1, R1, Q2, R2
  IC_74112 ic_74112_1 ();  // open: SET1, J1, CLK1, K1, CLR1, SET2, J2, CLK2, K2, CLR2, Q1, R1, Q2, R2
  IC_74161 ic_74161_1 ();  // open: CLK, CLR, LE, CEP, CET, D1, D2, D3, D4, Q1, Q2, Q3, Q4, TC
  IC_74377 ic_74377_1 ();  // open: D1, D2, D3, D4, D5, D6, D7, D8, CLK, CE, Y1, Y2, Y3, Y4, Y5, Y6, Y7, Y8
  IC_7403 ic_7403_1 ();  // open: A1, A2, A3, A4, B1, B2, B3, B4, Y1, Y2, Y3, Y4
  IC_7421 ic_7421_1 ();  // open: A1, A2, B1, B2, C1, C2, D1, D2, Y1, Y2
  IC_7475 ic_7475_1 ();  // open: D1, D2, D3, D4, LE12, LE34, Q1, R1, Q2, R2, Q3, R3, Q4, R4
  IC_74132 ic_74132_1 ();  // open: A1, A2, A3, A4, B1, B2, B3, B4, Y1, Y2, Y3, Y4
  IC_74163 ic_74163_1 ();  // open: CLK, CE, LE, CEP, CET, D1, D2, D3, D4, Q1, Q2, Q3, Q4, TC
  IC_7404 ic_7404_1 ();  // open: A1, A2, A3, A4, A5, A6, Y1, Y2, Y3, Y4, Y5, Y6
  IC_7427 ic_7427_1 ();  // open: A1, A2, A3, B1, B2, B3, C1, C2, C3, Y1, Y2, Y3
  IC_7476 ic_7476_1 ();  // open: SET1, J1, CLK1, K1, CLR1, SET2, J2, CLK2, K2, CLR2, Q1, R1, Q2, R2
  IC_74173 ic_74173_1 ();  // open: D1, D2, D3, D4, CLK, CE1, CE2, CLR, OE1, OE2, Q1, Q2, Q3, Q4
  IC_7405 ic_7405_1 ();  // open: A1, A2, A3, A4, A5, A6, Y1, Y2, Y3, Y4, Y5, Y6
  IC_7430 ic_7430_1 ();  // open: A, B, C, D, E, F, G, H, Y
  IC_7485 ic_7485_1 ();  // open: A4, B4, A3, B3, CLT, CEQ, CGT, A2, B2, A1, B1, YGT, YEQ, YLT
  IC_74138 ic_74138_1 ();  // open: A0, A1, A2, OE1, OE2, OE3, Y0, Y1, Y2, Y3, Y4, Y5, Y6, Y7
  IC_7408 ic_7408_1 ();  // open: A1, B1, A2, B2, A3, B3, A4, B4, Y1, Y2, Y3, Y4
  IC_7432 ic_7432_1 ();  // open: A1, B1, A2, B2, A3, B3, A4, B4, Y1, Y2, Y3, Y4
  IC_7486 ic_7486_1 ();  // open: A1, B1, A2, B2, A3, B3, A4, B4, Y1, Y2, Y3, Y4
  IC_74139 ic_74139_1 ();  // open: A0, A1, B0, B1, OEA, OEB, Y0, Y1, Y2, Y3, Z0, Z1, Z2, Z3
  IC_74175 ic_74175_1 ();  // open: D1, D2, D3, D4, CLK, CLR, Q1, R1, Q2, R2, Q3, R3, Q4, R4
  IC_74147 ic_74147_1 ();  // open: D1, D2, D3, D4, D5, D6, D7, D8, D9, Y1, Y2, Y3, Y4
  IC_74238 ic_74238_1 ();  // open: A0, A1, A2, OE1, OE2, OE3, Y0, Y1, Y2, Y3, Y4, Y5, Y6, Y7
  IC_7410 ic_7410_1 ();  // open: A1, A2, A3, B1, B2, B3, C1, C2, C3, Y1, Y2, Y3
  IC_7442 ic_7442_1 ();  // open: D1, D2, D3, D4, Y0, Y1, Y2, Y3, Y4, Y5, Y6, Y7, Y8, Y9
  IC_7493 ic_7493_1 ();  // open: CLK0, CLK1, CLR1, CLR2, Q1, Q2, Q3, Q4
  IC_74107 ic_74107_1 ();  // open: J1, CLK1, K1, CLR1, J2, CLK2, K2, CLR2, Q1, R1, Q2, R2
  IC_74151 ic_74151_1 ();  // open: A, B, C, D, E, F, G, J, S0, S1, S2, OE, Y, Z
  IC_74244 ic_74244_1 ();  // open: A1, A2, A3, A4, B1, B2, B3, B4, OEA, OEB, Y1, Y2, Y3, Y4, Z1, Z2, Z3, Z4
  IC_7411 ic_7411_1 ();  // open: A1, A2, B1, B2, C1, C2, Y1, Y2, Y3, C3, B3, A3
  IC_7451 ic_7451_1 ();  // open: A1, B1, C1, D1, E1, F1, A2, B2, C2, D2, Y1, Y2
  IC_74153 ic_74153_1 ();  // open: S0, S1, OE1, A1, B1, C1, D1, OE2, A2, B2, C2, D2, Y1, Y2
  IC_74273 ic_74273_1 ();  // open: CLR, CLK, D1, D2, D3, D4, D5, D6, D7, D8, Y1, Y2, Y3, Y4, Y6, Y7, Y8, Y5
  IC_74283 ic_74283_1 ();  // open: CIN, A1, B1, A2, B2, A3, B3, A4, B4, Y1, Y2, Y3, Y4, COUT

  // Notes on the sheet:
  //   Logisim 7400 series integrated circuits library
  //   Copyright (C) 2015 - 2018 by Stefan Rothe
  //   This library is licenced under the GNU Lesser General Public Licence version 3.
endmodule

module IC_7400 (
  input  A1,
  input  A2,
  input  A3,
  input  A4,
  input  B1,
  input  B2,
  input  B3,
  input  B4,
  output Y1,
  output Y2,
  output Y3,
  output Y4
);

  nand nand_1 (Y1, A1, B1);
  nand nand_2 (Y2, A2, B2);
  nand nand_3 (Y3, A3, B3);
  nand nand_4 (Y4, A4, B4);
endmodule

module IC_7402 (
  input  A1,
  input  A2,
  input  A3,
  input  A4,
  input  B1,
  input  B2,
  input  B3,
  input  B4,
  output Y1,
  output Y2,
  output Y3,
  output Y4
);

  nor nor_1 (Y1, A1, B1);
  nor nor_2 (Y2, A2, B2);
  nor nor_3 (Y3, A3, B3);
  nor nor_4 (Y4, A4, B4);
endmodule

module IC_7403 (
  input  A1,
  input  A2,
  input  A3,
  input  A4,
  input  B1,
  input  B2,
  input  B3,
  input  B4,
  output Y1,
  output Y2,
  output Y3,
  output Y4
);

  wire and_1_out, and_2_out, and_3_out, and_4_out;

  assign Y1 = and_1_out ? 1'b0 : 1'bz;  // Controlled_Buffer controlled_buffer_1
  and and_1 (and_1_out, A1, B1);
  assign Y2 = and_2_out ? 1'b0 : 1'bz;  // Controlled_Buffer controlled_buffer_2
  and and_2 (and_2_out, A2, B2);
  assign Y3 = and_3_out ? 1'b0 : 1'bz;  // Controlled_Buffer controlled_buffer_3
  and and_3 (and_3_out, A3, B3);
  assign Y4 = and_4_out ? 1'b0 : 1'bz;  // Controlled_Buffer controlled_buffer_4
  and and_4 (and_4_out, A4, B4);
endmodule

module IC_7404 (
  input  A1,
  input  A2,
  input  A3,
  input  A4,
  input  A5,
  input  A6,
  output Y1,
  output Y2,
  output Y3,
  output Y4,
  output Y5,
  output Y6
);

  not not_1 (Y1, A1);
  not not_2 (Y2, A2);
  not not_3 (Y3, A3);
  not not_4 (Y4, A4);
  not not_5 (Y5, A5);
  not not_6 (Y6, A6);
endmodule

module IC_7405 (
  input  A1,
  input  A2,
  input  A3,
  input  A4,
  input  A5,
  input  A6,
  output Y1,
  output Y2,
  output Y3,
  output Y4,
  output Y5,
  output Y6
);

  assign Y1 = A1 ? 1'b0 : 1'bz;  // Controlled_Buffer controlled_buffer_1
  assign Y2 = A2 ? 1'b0 : 1'bz;  // Controlled_Buffer controlled_buffer_2
  assign Y3 = A3 ? 1'b0 : 1'bz;  // Controlled_Buffer controlled_buffer_3
  assign Y4 = A4 ? 1'b0 : 1'bz;  // Controlled_Buffer controlled_buffer_4
  assign Y5 = A5 ? 1'b0 : 1'bz;  // Controlled_Buffer controlled_buffer_5
  assign Y6 = A6 ? 1'b0 : 1'bz;  // Controlled_Buffer controlled_buffer_6
endmodule

module IC_7408 (
  input  A1,
  input  A2,
  input  A3,
  input  A4,
  input  B1,
  input  B2,
  input  B3,
  input  B4,
  output Y1,
  output Y2,
  output Y3,
  output Y4
);

  and and_1 (Y1, A1, B1);
  and and_2 (Y2, A2, B2);
  and and_3 (Y3, A3, B3);
  and and_4 (Y4, A4, B4);
endmodule

module IC_7410 (
  input  A1,
  input  A2,
  input  A3,
  input  B1,
  input  B2,
  input  B3,
  input  C1,
  input  C2,
  input  C3,
  output Y1,
  output Y2,
  output Y3
);

  nand nand_1 (Y1, A1, B1, C1);
  nand nand_2 (Y2, A2, B2, C2);
  nand nand_3 (Y3, A3, B3, C3);
endmodule

module IC_7411 (
  input  A1,
  input  A2,
  input  A3,
  input  B1,
  input  B2,
  input  B3,
  input  C1,
  input  C2,
  input  C3,
  output Y1,
  output Y2,
  output Y3
);

  and and_1 (Y1, A1, B1, C1);
  and and_2 (Y2, A2, B2, C2);
  and and_3 (Y3, A3, B3, C3);
endmodule

module IC_7414 (
  input  A1,
  input  A2,
  input  A3,
  input  A4,
  input  A5,
  input  A6,
  output Y1,
  output Y2,
  output Y3,
  output Y4,
  output Y5,
  output Y6
);

  not not_1 (Y1, A1);
  not not_2 (Y2, A2);
  not not_3 (Y3, A3);
  not not_4 (Y4, A4);
  not not_5 (Y5, A5);
  not not_6 (Y6, A6);
endmodule

module IC_7420 (
  input  A1,
  input  A2,
  input  B1,
  input  B2,
  input  C1,
  input  C2,
  input  D1,
  input  D2,
  output Y1,
  output Y2
);

  nand nand_1 (Y1, A1, B1, C1, D1);
  nand nand_2 (Y2, A2, B2, C2, D2);
endmodule

module IC_7421 (
  input  A1,
  input  A2,
  input  B1,
  input  B2,
  input  C1,
  input  C2,
  input  D1,
  input  D2,
  output Y1,
  output Y2
);

  and and_1 (Y1, A1, B1, C1, D1);
  and and_2 (Y2, A2, B2, C2, D2);
endmodule

module IC_7427 (
  input  A1,
  input  A2,
  input  A3,
  input  B1,
  input  B2,
  input  B3,
  input  C1,
  input  C2,
  input  C3,
  output Y1,
  output Y2,
  output Y3
);

  nor nor_1 (Y1, A1, B1, C1);
  nor nor_2 (Y2, A2, B2, C2);
  nor nor_3 (Y3, A3, B3, C3);
endmodule

module IC_7430 (
  input  A,
  input  B,
  input  C,
  input  D,
  input  E,
  input  F,
  input  G,
  input  H,
  output Y
);

  nand nand_1 (Y, A, B, C, D, E, F, G, H);
endmodule

module IC_7432 (
  input  A1,
  input  A2,
  input  A3,
  input  A4,
  input  B1,
  input  B2,
  input  B3,
  input  B4,
  output Y1,
  output Y2,
  output Y3,
  output Y4
);

  or or_1 (Y1, A1, B1);
  or or_2 (Y2, A2, B2);
  or or_3 (Y3, A3, B3);
  or or_4 (Y4, A4, B4);
endmodule

module IC_7442 (
  input  D1,
  input  D2,
  input  D3,
  input  D4,
  output Y0,
  output Y1,
  output Y2,
  output Y3,
  output Y4,
  output Y5,
  output Y6,
  output Y7,
  output Y8,
  output Y9
);

  wire nand_1_out, nand_2_out, nand_3_out, nand_4_out, nand_5_out, nand_6_out, nand_7_out, not_1_out,
       not_2_out, not_3_out, not_4_out, not_5_out, not_6_out, not_7_out, not_8_out;

  not not_1 (not_1_out, D1);
  not not_2 (not_2_out, D2);
  not not_3 (not_3_out, D3);
  not not_4 (not_4_out, D4);
  not not_5 (not_5_out, not_1_out);
  not not_6 (not_6_out, not_2_out);
  not not_7 (not_7_out, not_3_out);
  not not_8 (not_8_out, not_4_out);
  nand nand_1 (nand_1_out, not_1_out, not_2_out);
  nand nand_2 (nand_2_out, not_5_out, not_2_out);
  nand nand_3 (nand_3_out, not_1_out, not_6_out);
  nand nand_4 (nand_4_out, not_5_out, not_6_out);
  nand nand_5 (nand_5_out, not_3_out, not_4_out);
  nand nand_6 (nand_6_out, not_7_out, not_4_out);
  nand nand_7 (nand_7_out, not_3_out, not_8_out);
  nand nand_8 (Y0, ~nand_1_out, ~nand_5_out);  // NAND_Gate
  nand nand_9 (Y1, ~nand_2_out, ~nand_5_out);  // NAND_Gate
  nand nand_10 (Y2, ~nand_3_out, ~nand_5_out);  // NAND_Gate
  nand nand_11 (Y3, ~nand_4_out, ~nand_5_out);  // NAND_Gate
  nand nand_12 (Y4, ~nand_1_out, ~nand_6_out);  // NAND_Gate
  nand nand_13 (Y5, ~nand_2_out, ~nand_6_out);  // NAND_Gate
  nand nand_14 (Y6, ~nand_3_out, ~nand_6_out);  // NAND_Gate
  nand nand_15 (Y7, ~nand_4_out, ~nand_6_out);  // NAND_Gate
  nand nand_16 (Y8, ~nand_1_out, ~nand_7_out);  // NAND_Gate
  nand nand_17 (Y9, ~nand_2_out, ~nand_7_out);  // NAND_Gate
endmodule

module IC_7451 (
  input  A1,
  input  B1,
  input  C1,
  input  D1,
  input  E1,
  input  F1,
  input  A2,
  input  B2,
  input  C2,
  input  D2,
  output Y1,
  output Y2
);

  wire and_1_out, and_2_out, and_3_out, and_4_out;

  and and_1 (and_1_out, A1, B1, C1);
  and and_2 (and_2_out, D1, E1, F1);
  and and_3 (and_3_out, A2, B2);
  and and_4 (and_4_out, C2, D2);
  nor nor_1 (Y1, and_1_out, and_2_out);
  nor nor_2 (Y2, and_3_out, and_4_out);
endmodule

module IC_7473 (
  input  J1,
  input  CLK1,
  input  K1,
  input  CLR1,
  input  J2,
  input  CLK2,
  input  K2,
  input  CLR2,
  output Q1,
  output R1,
  output Q2,
  output R2
);

  wire not_1_out, not_2_out, not_3_out, not_4_out;

  not not_1 (not_1_out, CLK1);
  not not_2 (not_2_out, CLR1);
  not not_3 (not_3_out, CLK2);
  not not_4 (not_4_out, CLR2);
  JK_Flip_Flop jk_flip_flop_1 (.J(J1), .CLK(not_1_out), .K(K1), .Q(Q1), .R(R1), .CLR(not_2_out));  // open: SET
  JK_Flip_Flop jk_flip_flop_2 (.J(J2), .CLK(not_3_out), .K(K2), .Q(Q2), .R(R2), .CLR(not_4_out));  // open: SET
endmodule

module IC_7474 (
  input  SET1,
  input  D1,
  input  CLK1,
  input  CLR1,
  input  SET2,
  input  D2,
  input  CLK2,
  input  CLR2,
  output Q1,
  output R1,
  output Q2,
  output R2
);

  wire not_1_out, not_2_out, not_3_out, not_4_out;

  not not_1 (not_1_out, SET1);
  D_Flip_Flop d_flip_flop_1 (.D(D1), .CLK(CLK1), .Q(Q1), .R(R1), .SET(not_1_out), .CLR(not_2_out));
  not not_2 (not_2_out, CLR1);
  not not_3 (not_3_out, SET2);
  D_Flip_Flop d_flip_flop_2 (.D(D2), .CLK(CLK2), .Q(Q2), .R(R2), .SET(not_3_out), .CLR(not_4_out));
  not not_4 (not_4_out, CLR2);
endmodule

module IC_7475 (
  input  D1,
  input  D2,
  input  LE12,
  input  D3,
  input  D4,
  input  LE34,
  output Q1,
  output R1,
  output Q2,
  output R2,
  output Q3,
  output R3,
  output Q4,
  output R4
);

  D_Latch d_latch_1 (.D(D1), .LE(LE12), .Q(Q1), .R(R1));  // open: SET, CLR
  D_Latch d_latch_2 (.D(D2), .LE(LE12), .Q(Q2), .R(R2));  // open: SET, CLR
  D_Latch d_latch_3 (.D(D3), .LE(LE34), .Q(Q3), .R(R3));  // open: SET, CLR
  D_Latch d_latch_4 (.D(D4), .LE(LE34), .Q(Q4), .R(R4));  // open: SET, CLR
endmodule

module IC_7476 (
  input  SET1,
  input  J1,
  input  CLK1,
  input  K1,
  input  CLR1,
  input  SET2,
  input  J2,
  input  CLK2,
  input  K2,
  input  CLR2,
  output Q1,
  output R1,
  output Q2,
  output R2
);

  wire not_1_out, not_2_out, not_3_out, not_4_out, not_5_out, not_6_out;

  not not_1 (not_1_out, SET1);
  not not_2 (not_2_out, CLK1);
  not not_3 (not_3_out, CLR1);
  not not_4 (not_4_out, SET2);
  not not_5 (not_5_out, CLK2);
  not not_6 (not_6_out, CLR2);
  JK_Flip_Flop jk_flip_flop_1 (.J(J1), .CLK(not_2_out), .K(K1), .Q(Q1), .R(R1), .SET(not_1_out), .CLR(not_3_out));
  JK_Flip_Flop jk_flip_flop_2 (.J(J2), .CLK(not_5_out), .K(K2), .Q(Q2), .R(R2), .SET(not_4_out), .CLR(not_6_out));
endmodule

module IC_7485 (
  input  A1,
  input  A2,
  input  A3,
  input  A4,
  input  B1,
  input  B2,
  input  B3,
  input  B4,
  input  CLT,
  input  CEQ,
  input  CGT,
  output YLT,
  output YEQ,
  output YGT
);

  wire and_1_out, and_2_out, and_3_out, and_4_out, and_5_out, and_6_out, and_7_out, and_8_out, and_9_out,
       and_10_out, and_11_out, and_12_out, and_13_out, and_14_out, and_16_out, and_17_out, and_18_out,
       and_19_out, and_20_out, and_21_out, nand_1_out, nand_2_out, nand_3_out, nand_4_out, nor_1_out,
       nor_2_out, nor_3_out, nor_4_out;

  nand nand_1 (nand_1_out, A4, B4);
  nand nand_2 (nand_2_out, A3, B3);
  nand nand_3 (nand_3_out, A2, B2);
  nand nand_4 (nand_4_out, A1, B1);
  and and_1 (and_1_out, A4, nand_1_out);
  and and_2 (and_2_out, nand_1_out, B4);
  and and_3 (and_3_out, A3, nand_2_out);
  and and_4 (and_4_out, nand_2_out, B3);
  and and_5 (and_5_out, A2, nand_3_out);
  and and_6 (and_6_out, nand_3_out, B2);
  and and_7 (and_7_out, A1, nand_4_out);
  and and_8 (and_8_out, nand_4_out, B1);
  nor nor_1 (nor_1_out, and_1_out, and_2_out);
  nor nor_2 (nor_2_out, and_3_out, and_4_out);
  nor nor_3 (nor_3_out, and_5_out, and_6_out);
  nor nor_4 (nor_4_out, and_7_out, and_8_out);
  and and_9 (and_9_out, B4, nand_1_out);
  and and_10 (and_10_out, B3, nand_2_out, nor_1_out);
  and and_11 (and_11_out, B2, nand_3_out, nor_1_out, nor_2_out);
  and and_12 (and_12_out, B1, nand_4_out, nor_1_out, nor_2_out, nor_3_out);
  and and_13 (and_13_out, nor_1_out, nor_2_out, nor_3_out, nor_4_out, CLT);
  and and_14 (and_14_out, nor_1_out, nor_2_out, nor_3_out, nor_4_out, CEQ);
  and and_15 (YEQ, nor_1_out, nor_2_out, CEQ, nor_3_out, nor_4_out);
  and and_16 (and_16_out, CEQ, nor_4_out, nor_3_out, nor_2_out, nor_1_out);
  and and_17 (and_17_out, CGT, nor_4_out, nor_3_out, nor_2_out, nor_1_out);
  and and_18 (and_18_out, nor_3_out, nor_2_out, nor_1_out, nand_4_out, A1);
  and and_19 (and_19_out, nor_2_out, nor_1_out, nand_3_out, A2);
  and and_20 (and_20_out, nor_1_out, nand_2_out, A3);
  and and_21 (and_21_out, nand_1_out, A4);
  nor nor_5 (YGT, and_9_out, and_10_out, and_11_out, and_12_out, and_13_out, and_14_out);
  nor nor_6 (YLT, and_16_out, and_17_out, and_18_out, and_19_out, and_20_out, and_21_out);
endmodule

module IC_7486 (
  input  A1,
  input  A2,
  input  A3,
  input  A4,
  input  B1,
  input  B2,
  input  B3,
  input  B4,
  output Y1,
  output Y2,
  output Y3,
  output Y4
);

  xor xor_1 (Y1, A1, B1);
  xor xor_2 (Y2, A2, B2);
  xor xor_3 (Y3, A3, B3);
  xor xor_4 (Y4, A4, B4);
endmodule

module IC_7493 (
  input  CLK0,
  input  CLK1,
  input  CLR1,
  input  CLR2,
  output Q1,
  output Q2,
  output Q3,
  output Q4
);

  wire and_1_out, d_flip_flop_1_r, d_flip_flop_2_r, d_flip_flop_3_r, d_flip_flop_4_r, not_1_out, not_2_out,
       not_3_out, not_4_out;

  not not_1 (not_1_out, CLK0);
  not not_2 (not_2_out, CLK1);
  and and_1 (and_1_out, CLR1, CLR2);
  not not_3 (not_3_out, Q2);
  not not_4 (not_4_out, Q3);
  D_Flip_Flop d_flip_flop_1 (
    .D(d_flip_flop_1_r), .CLK(not_1_out), .Q(Q1), .R(d_flip_flop_1_r), .CLR(and_1_out));  // open: SET
  D_Flip_Flop d_flip_flop_2 (
    .D(d_flip_flop_2_r), .CLK(not_2_out), .Q(Q2), .R(d_flip_flop_2_r), .CLR(and_1_out));  // open: SET
  D_Flip_Flop d_flip_flop_3 (
    .D(d_flip_flop_3_r), .CLK(not_3_out), .Q(Q3), .R(d_flip_flop_3_r), .CLR(and_1_out));  // open: SET
  D_Flip_Flop d_flip_flop_4 (.D(d_flip_flop_4_r), .CLK(not_4_out), .Q(Q4), .R(d_flip_flop_4_r));  // open: SET, CLR
endmodule

module IC_74107 (
  input  J1,
  input  CLK1,
  input  K1,
  input  CLR1,
  input  J2,
  input  CLK2,
  input  K2,
  input  CLR2,
  output Q1,
  output R1,
  output Q2,
  output R2
);

  wire not_1_out, not_2_out, not_3_out, not_4_out;

  not not_1 (not_1_out, K1);
  not not_2 (not_2_out, CLR1);
  not not_3 (not_3_out, K2);
  not not_4 (not_4_out, CLR2);
  JK_Flip_Flop jk_flip_flop_1 (.J(J1), .CLK(CLK1), .K(not_1_out), .Q(Q1), .R(R1), .CLR(not_2_out));  // open: SET
  JK_Flip_Flop jk_flip_flop_2 (.J(J2), .CLK(CLK2), .K(not_3_out), .Q(Q2), .R(R2), .CLR(not_4_out));  // open: SET
endmodule

module IC_74109 (
  input  SET1,
  input  J1,
  input  CLK1,
  input  K1,
  input  CLR1,
  input  SET2,
  input  J2,
  input  CLK2,
  input  K2,
  input  CLR2,
  output Q1,
  output R1,
  output Q2,
  output R2
);

  wire not_1_out, not_2_out, not_3_out, not_4_out, not_5_out, not_6_out;

  not not_1 (not_1_out, SET1);
  not not_2 (not_2_out, K1);
  not not_3 (not_3_out, CLR1);
  not not_4 (not_4_out, SET2);
  not not_5 (not_5_out, K2);
  not not_6 (not_6_out, CLR2);
  JK_Flip_Flop jk_flip_flop_1 (.J(J1), .CLK(CLK1), .K(not_2_out), .Q(Q1), .R(R1), .SET(not_1_out), .CLR(not_3_out));
  JK_Flip_Flop jk_flip_flop_2 (.J(J2), .CLK(CLK2), .K(not_5_out), .Q(Q2), .R(R2), .SET(not_4_out), .CLR(not_6_out));
endmodule

module IC_74112 (
  input  SET1,
  input  J1,
  input  CLK1,
  input  K1,
  input  CLR1,
  input  SET2,
  input  J2,
  input  CLK2,
  input  K2,
  input  CLR2,
  output Q1,
  output R1,
  output Q2,
  output R2
);

  wire not_1_out, not_2_out, not_3_out, not_4_out, not_5_out, not_6_out;

  not not_1 (not_1_out, SET1);
  not not_2 (not_2_out, CLK1);
  not not_3 (not_3_out, CLR1);
  not not_4 (not_4_out, SET2);
  not not_5 (not_5_out, CLK2);
  not not_6 (not_6_out, CLR2);
  JK_Flip_Flop jk_flip_flop_1 (.J(J1), .CLK(not_2_out), .K(K1), .Q(Q1), .R(R1), .SET(not_1_out), .CLR(not_3_out));
  JK_Flip_Flop jk_flip_flop_2 (.J(J2), .CLK(not_5_out), .K(K2), .Q(Q2), .R(R2), .SET(not_4_out), .CLR(not_6_out));
endmodule

module IC_74132 (
  input  A1,
  input  A2,
  input  A3,
  input  A4,
  input  B1,
  input  B2,
  input  B3,
  input  B4,
  output Y1,
  output Y2,
  output Y3,
  output Y4
);

  nand nand_1 (Y1, A1, B1);
  nand nand_2 (Y2, A2, B2);
  nand nand_3 (Y3, A3, B3);
  nand nand_4 (Y4, A4, B4);
endmodule

module IC_74138 (
  input  A0,
  input  A1,
  input  A2,
  input  OE1,
  input  OE2,
  input  OE3,
  output Y0,
  output Y1,
  output Y2,
  output Y3,
  output Y4,
  output Y5,
  output Y6,
  output Y7
);

  wire and_1_out, not_1_out, not_2_out, not_3_out, not_4_out, not_5_out;

  not not_1 (not_1_out, A0);
  not not_2 (not_2_out, A1);
  not not_3 (not_3_out, A2);
  not not_4 (not_4_out, OE1);
  not not_5 (not_5_out, OE2);
  and and_1 (and_1_out, not_4_out, not_5_out, OE3);
  nand nand_1 (Y0, not_1_out, not_2_out, not_3_out, and_1_out);
  nand nand_2 (Y1, A0, not_2_out, not_3_out, and_1_out);
  nand nand_3 (Y2, not_1_out, A1, not_3_out, and_1_out);
  nand nand_4 (Y3, A0, A1, not_3_out, and_1_out);
  nand nand_5 (Y4, not_1_out, not_2_out, A2, and_1_out);
  nand nand_6 (Y5, A0, not_2_out, A2, and_1_out);
  nand nand_7 (Y6, not_1_out, A1, A2, and_1_out);
  nand nand_8 (Y7, A0, A1, A2, and_1_out);
endmodule

module IC_74139 (
  input  A0,
  input  A1,
  input  OEA,
  input  B0,
  input  B1,
  input  OEB,
  output Y0,
  output Y1,
  output Y2,
  output Y3,
  output Z0,
  output Z1,
  output Z2,
  output Z3
);

  wire not_1_out, not_2_out, not_3_out, not_4_out, not_5_out, not_6_out;

  not not_1 (not_1_out, A0);
  not not_2 (not_2_out, A1);
  not not_3 (not_3_out, OEA);
  not not_4 (not_4_out, B0);
  not not_5 (not_5_out, B1);
  not not_6 (not_6_out, OEB);
  nand nand_1 (Y0, not_1_out, not_2_out, not_3_out);
  nand nand_2 (Y1, A0, not_2_out, not_3_out);
  nand nand_3 (Y2, not_1_out, A1, not_3_out);
  nand nand_4 (Y3, A0, A1, not_3_out);
  nand nand_5 (Z0, not_4_out, not_5_out, not_6_out);
  nand nand_6 (Z1, B0, not_5_out, not_6_out);
  nand nand_7 (Z2, not_4_out, B1, not_6_out);
  nand nand_8 (Z3, B0, B1, not_6_out);
endmodule

module IC_74147 (
  input  D1,
  input  D2,
  input  D3,
  input  D4,
  input  D5,
  input  D6,
  input  D7,
  input  D8,
  input  D9,
  output Y1,
  output Y2,
  output Y3,
  output Y4
);

  wire and_1_out, and_2_out, and_3_out, and_4_out, and_5_out, and_6_out, and_7_out, and_8_out, and_9_out,
       and_10_out, and_11_out, and_12_out, buffer_1_out, nor_1_out, not_1_out, not_2_out, not_3_out,
       not_4_out, not_5_out, not_6_out, not_7_out, not_8_out, not_9_out, not_10_out, not_11_out, not_12_out,
       not_13_out;

  not not_1 (not_1_out, D1);
  not not_2 (not_2_out, D2);
  not not_3 (not_3_out, D3);
  not not_4 (not_4_out, D4);
  not not_5 (not_5_out, D5);
  not not_6 (not_6_out, D6);
  not not_7 (not_7_out, D7);
  not not_8 (not_8_out, D8);
  not not_9 (not_9_out, D9);
  not not_10 (not_10_out, not_2_out);
  not not_11 (not_11_out, not_4_out);
  not not_12 (not_12_out, not_5_out);
  not not_13 (not_13_out, not_6_out);
  nor nor_1 (nor_1_out, not_8_out, not_9_out);
  and and_1 (and_1_out, not_1_out, not_10_out, not_11_out, not_13_out, nor_1_out);
  and and_2 (and_2_out, not_3_out, not_11_out, not_13_out, nor_1_out);
  and and_3 (and_3_out, not_5_out, not_13_out, nor_1_out);
  and and_4 (and_4_out, not_7_out, nor_1_out);
  buf buffer_1 (buffer_1_out, not_9_out);
  and and_5 (and_5_out, not_2_out, not_11_out, not_12_out, nor_1_out);
  and and_6 (and_6_out, not_3_out, not_11_out, not_12_out, nor_1_out);
  and and_7 (and_7_out, not_6_out, nor_1_out);
  and and_8 (and_8_out, not_7_out, nor_1_out);
  and and_9 (and_9_out, not_4_out, nor_1_out);
  and and_10 (and_10_out, not_5_out, nor_1_out);
  and and_11 (and_11_out, not_6_out, nor_1_out);
  and and_12 (and_12_out, not_7_out, nor_1_out);
  nor nor_2 (Y1, and_1_out, and_2_out, and_3_out, and_4_out, buffer_1_out);
  nor nor_3 (Y2, and_5_out, and_6_out, and_7_out, and_8_out);
  nor nor_4 (Y3, and_9_out, and_10_out, and_11_out, and_12_out);
  nor nor_5 (Y4, not_8_out, not_9_out);
endmodule

module IC_74151 (
  input  A,
  input  B,
  input  C,
  input  D,
  input  E,
  input  F,
  input  G,
  input  J,
  input  S0,
  input  S1,
  input  S2,
  input  OE,
  output Y,
  output Z
);

  wire and_1_out, and_2_out, and_3_out, and_4_out, and_5_out, and_6_out, and_7_out, and_8_out, not_1_out,
       not_2_out, not_3_out, not_4_out;

  not not_1 (not_1_out, S1);
  not not_2 (not_2_out, S0);
  not not_3 (not_3_out, OE);
  not not_4 (not_4_out, S2);
  and and_1 (and_1_out, A, not_3_out, not_2_out, not_1_out, not_4_out);
  and and_2 (and_2_out, B, not_3_out, S0, not_1_out, not_4_out);
  and and_3 (and_3_out, C, not_3_out, not_2_out, S1, not_4_out);
  and and_4 (and_4_out, D, not_3_out, S0, S1, not_4_out);
  and and_5 (and_5_out, E, not_3_out, not_2_out, not_1_out, S2);
  and and_6 (and_6_out, F, not_3_out, S0, not_1_out, S2);
  and and_7 (and_7_out, G, not_3_out, not_2_out, S1, S2);
  and and_8 (and_8_out, J, not_3_out, S0, S1, S2);
  or or_1 (Y, and_1_out, and_2_out, and_3_out, and_4_out, and_5_out, and_6_out, and_7_out, and_8_out);
  not not_5 (Z, Y);
endmodule

module IC_74153 (
  input  A1,
  input  B1,
  input  C1,
  input  D1,
  input  A2,
  input  B2,
  input  C2,
  input  D2,
  input  S0,
  input  S1,
  input  OE1,
  input  OE2,
  output Y1,
  output Y2
);

  wire and_1_out, and_2_out, and_3_out, and_4_out, and_5_out, and_6_out, and_7_out, and_8_out, not_1_out,
       not_2_out, not_3_out, not_4_out;

  not not_1 (not_1_out, S1);
  not not_2 (not_2_out, S0);
  not not_3 (not_3_out, OE1);
  not not_4 (not_4_out, OE2);
  and and_1 (and_1_out, A1, not_3_out, not_2_out, not_1_out);
  and and_2 (and_2_out, B1, not_3_out, S0, not_1_out);
  and and_3 (and_3_out, C1, not_3_out, not_2_out, S1);
  and and_4 (and_4_out, D1, not_3_out, S0, S1);
  and and_5 (and_5_out, A2, not_4_out, not_2_out, not_1_out);
  and and_6 (and_6_out, B2, not_4_out, S0, not_1_out);
  and and_7 (and_7_out, C2, not_4_out, not_2_out, S1);
  and and_8 (and_8_out, D2, not_4_out, S0, S1);
  or or_1 (Y1, and_1_out, and_2_out, and_3_out, and_4_out);
  or or_2 (Y2, and_5_out, and_6_out, and_7_out, and_8_out);
endmodule

module IC_74157 (
  input  A1,
  input  B1,
  input  A2,
  input  B2,
  input  A3,
  input  B3,
  input  A4,
  input  B4,
  input  S0,
  input  OE,
  output Y1,
  output Y2,
  output Y3,
  output Y4
);

  wire and_1_out, and_2_out, and_3_out, and_4_out, and_5_out, and_6_out, and_7_out, and_8_out, not_1_out,
       not_2_out;

  not not_1 (not_1_out, S0);
  not not_2 (not_2_out, OE);
  and and_1 (and_1_out, A1, not_1_out, not_2_out);
  and and_2 (and_2_out, B1, S0, not_2_out);
  and and_3 (and_3_out, A2, not_1_out, not_2_out);
  and and_4 (and_4_out, B2, S0, not_2_out);
  and and_5 (and_5_out, A3, not_1_out, not_2_out);
  and and_6 (and_6_out, B3, S0, not_2_out);
  and and_7 (and_7_out, A4, not_1_out, not_2_out);
  and and_8 (and_8_out, B4, S0, not_2_out);
  or or_1 (Y1, and_1_out, and_2_out);
  or or_2 (Y2, and_3_out, and_4_out);
  or or_3 (Y3, and_5_out, and_6_out);
  or or_4 (Y4, and_7_out, and_8_out);
endmodule

module IC_74161 (
  input  CLK,
  input  CLR,
  input  LE,
  input  CEP,
  input  CET,
  input  D1,
  input  D2,
  input  D3,
  input  D4,
  output Q1,
  output Q2,
  output Q3,
  output Q4,
  output TC
);

  wire and_1_out, and_2_out, and_3_out, and_4_out, and_5_out, and_6_out, and_7_out, and_8_out, and_9_out,
       and_10_out, and_11_out, and_12_out, not_1_out, not_2_out, not_3_out, or_1_out, or_2_out, or_3_out,
       or_4_out, xor_1_out, xor_2_out, xor_3_out, xor_4_out;

  not not_1 (not_1_out, CLK);
  not not_2 (not_2_out, CLR);
  and and_1 (and_1_out, LE, CEP, CET);
  not not_3 (not_3_out, LE);
  and and_2 (and_2_out, D1, not_3_out);
  and and_3 (and_3_out, Q1, LE);
  and and_4 (and_4_out, D2, not_3_out);
  and and_5 (and_5_out, Q2, LE);
  and and_6 (and_6_out, Q1, and_1_out);
  and and_7 (and_7_out, D3, not_3_out);
  and and_8 (and_8_out, Q3, LE);
  and and_9 (and_9_out, Q2, Q1, and_1_out);
  and and_10 (and_10_out, D4, not_3_out);
  and and_11 (and_11_out, Q4, LE);
  and and_12 (and_12_out, Q3, Q2, Q1, and_1_out);
  xor xor_1 (xor_1_out, and_3_out, and_1_out);
  xor xor_2 (xor_2_out, and_5_out, and_6_out);
  xor xor_3 (xor_3_out, and_8_out, and_9_out);
  xor xor_4 (xor_4_out, and_11_out, and_12_out);
  or or_1 (or_1_out, and_2_out, xor_1_out);
  or or_2 (or_2_out, and_4_out, xor_2_out);
  or or_3 (or_3_out, and_7_out, xor_3_out);
  or or_4 (or_4_out, and_10_out, xor_4_out);
  D_Flip_Flop d_flip_flop_1 (.D(or_1_out), .CLK(not_1_out), .Q(Q1), .CLR(not_2_out));  // open: R, SET
  D_Flip_Flop d_flip_flop_2 (.D(or_2_out), .CLK(not_1_out), .Q(Q2), .CLR(not_2_out));  // open: R, SET
  D_Flip_Flop d_flip_flop_3 (.D(or_3_out), .CLK(not_1_out), .Q(Q3), .CLR(not_2_out));  // open: R, SET
  D_Flip_Flop d_flip_flop_4 (.D(or_4_out), .CLK(not_1_out), .Q(Q4), .CLR(not_2_out));  // open: R, SET
  and and_13 (TC, Q4, Q3, Q2, Q1, CET);
endmodule

module IC_74163 (
  input  CLK,
  input  CE,
  input  LE,
  input  CEP,
  input  CET,
  input  D1,
  input  D2,
  input  D3,
  input  D4,
  output Q1,
  output Q2,
  output Q3,
  output Q4,
  output TC
);

  wire and_1_out, and_2_out, and_3_out, and_4_out, and_5_out, and_6_out, and_7_out, and_8_out, and_9_out,
       and_10_out, and_11_out, and_12_out, and_13_out, not_1_out, not_2_out, not_3_out, or_1_out, or_2_out,
       or_3_out, or_4_out, xor_1_out, xor_2_out, xor_3_out, xor_4_out;

  not not_1 (not_1_out, CLK);
  not not_2 (not_2_out, CE);
  and and_1 (and_1_out, LE, CEP, CET);
  not not_3 (not_3_out, LE);
  and and_2 (and_2_out, D1, not_2_out, not_3_out);
  and and_3 (and_3_out, Q1, not_2_out, LE);
  and and_4 (and_4_out, not_2_out, and_1_out);
  and and_5 (and_5_out, D2, not_2_out, not_3_out);
  and and_6 (and_6_out, Q2, not_2_out, LE);
  and and_7 (and_7_out, Q1, not_2_out, and_1_out);
  and and_8 (and_8_out, D3, not_2_out, not_3_out);
  and and_9 (and_9_out, Q3, not_2_out, LE);
  and and_10 (and_10_out, Q2, Q1, and_1_out, not_2_out);
  and and_11 (and_11_out, D4, not_2_out, not_3_out);
  and and_12 (and_12_out, Q4, not_2_out, LE);
  and and_13 (and_13_out, Q3, Q2, not_2_out, Q1, and_1_out);
  xor xor_1 (xor_1_out, and_3_out, and_4_out);
  xor xor_2 (xor_2_out, and_6_out, and_7_out);
  xor xor_3 (xor_3_out, and_9_out, and_10_out);
  xor xor_4 (xor_4_out, and_12_out, and_13_out);
  or or_1 (or_1_out, and_2_out, xor_1_out);
  or or_2 (or_2_out, and_5_out, xor_2_out);
  or or_3 (or_3_out, and_8_out, xor_3_out);
  or or_4 (or_4_out, and_11_out, xor_4_out);
  D_Flip_Flop d_flip_flop_1 (.D(or_1_out), .CLK(not_1_out), .Q(Q1));  // open: R, SET, CLR
  D_Flip_Flop d_flip_flop_2 (.D(or_2_out), .CLK(not_1_out), .Q(Q2));  // open: R, SET, CLR
  D_Flip_Flop d_flip_flop_3 (.D(or_3_out), .CLK(not_1_out), .Q(Q3));  // open: R, SET, CLR
  D_Flip_Flop d_flip_flop_4 (.D(or_4_out), .CLK(not_1_out), .Q(Q4));  // open: R, SET, CLR
  and and_14 (TC, Q4, Q3, Q2, Q1, CET);
endmodule

module IC_74173 (
  input  D1,
  input  D2,
  input  D3,
  input  D4,
  input  CLK,
  input  CE1,
  input  CE2,
  input  CLR,
  input  OE1,
  input  OE2,
  output Q1,
  output Q2,
  output Q3,
  output Q4
);

  wire and_1_out, d_flip_flop_1_q, d_flip_flop_2_q, d_flip_flop_3_q, d_flip_flop_4_q, nor_1_out, nor_2_out;

  nor nor_1 (nor_1_out, CE1, CE2);
  nor nor_2 (nor_2_out, OE1, OE2);
  and and_1 (and_1_out, CLK, nor_1_out);
  D_Flip_Flop d_flip_flop_1 (.D(D1), .CLK(and_1_out), .Q(d_flip_flop_1_q), .CLR(CLR));  // open: R, SET
  D_Flip_Flop d_flip_flop_2 (.D(D2), .CLK(and_1_out), .Q(d_flip_flop_2_q), .CLR(CLR));  // open: R, SET
  D_Flip_Flop d_flip_flop_3 (.D(D3), .CLK(and_1_out), .Q(d_flip_flop_3_q), .CLR(CLR));  // open: R, SET
  D_Flip_Flop d_flip_flop_4 (.D(D4), .CLK(and_1_out), .Q(d_flip_flop_4_q), .CLR(CLR));  // open: R, SET
  assign Q1 = nor_2_out ? d_flip_flop_1_q : 1'bz;  // Controlled_Buffer controlled_buffer_1
  assign Q2 = nor_2_out ? d_flip_flop_2_q : 1'bz;  // Controlled_Buffer controlled_buffer_2
  assign Q3 = nor_2_out ? d_flip_flop_3_q : 1'bz;  // Controlled_Buffer controlled_buffer_3
  assign Q4 = nor_2_out ? d_flip_flop_4_q : 1'bz;  // Controlled_Buffer controlled_buffer_4
endmodule

module IC_74175 (
  input  D1,
  input  D2,
  input  D3,
  input  D4,
  input  CLK,
  input  CLR,
  output Q1,
  output R1,
  output Q2,
  output R2,
  output Q3,
  output R3,
  output Q4,
  output R4
);

  wire not_1_out;

  not not_1 (not_1_out, CLR);
  D_Flip_Flop d_flip_flop_1 (.D(D1), .CLK(CLK), .Q(Q1), .R(R1), .CLR(not_1_out));  // open: SET
  D_Flip_Flop d_flip_flop_2 (.D(D2), .CLK(CLK), .Q(Q2), .R(R2), .CLR(not_1_out));  // open: SET
  D_Flip_Flop d_flip_flop_3 (.D(D3), .CLK(CLK), .Q(Q3), .R(R3), .CLR(not_1_out));  // open: SET
  D_Flip_Flop d_flip_flop_4 (.D(D4), .CLK(CLK), .Q(Q4), .R(R4), .CLR(not_1_out));  // open: SET
endmodule

module IC_74238 (
  input  A0,
  input  A1,
  input  A2,
  input  OE1,
  input  OE2,
  input  OE3,
  output Y0,
  output Y1,
  output Y2,
  output Y3,
  output Y4,
  output Y5,
  output Y6,
  output Y7
);

  wire and_1_out, not_1_out, not_2_out, not_3_out, not_4_out, not_5_out;

  not not_1 (not_1_out, A0);
  not not_2 (not_2_out, A1);
  not not_3 (not_3_out, A2);
  not not_4 (not_4_out, OE1);
  not not_5 (not_5_out, OE2);
  and and_1 (and_1_out, not_4_out, not_5_out, OE3);
  and and_2 (Y0, not_1_out, not_2_out, not_3_out, and_1_out);
  and and_3 (Y1, A0, not_2_out, not_3_out, and_1_out);
  and and_4 (Y2, not_1_out, A1, not_3_out, and_1_out);
  and and_5 (Y3, A0, A1, not_3_out, and_1_out);
  and and_6 (Y4, not_1_out, not_2_out, A2, and_1_out);
  and and_7 (Y5, A0, not_2_out, A2, and_1_out);
  and and_8 (Y6, not_1_out, A1, A2, and_1_out);
  and and_9 (Y7, A0, A1, A2, and_1_out);
endmodule

module IC_74244 (
  input  A1,
  input  A2,
  input  A3,
  input  A4,
  input  OEA,
  input  B1,
  input  B2,
  input  B3,
  input  B4,
  input  OEB,
  output Y1,
  output Y2,
  output Y3,
  output Y4,
  output Z1,
  output Z2,
  output Z3,
  output Z4
);

  wire not_1_out, not_2_out;

  not not_1 (not_1_out, OEA);
  not not_2 (not_2_out, OEB);
  assign Y1 = not_1_out ? A1 : 1'bz;  // Controlled_Buffer controlled_buffer_1
  assign Y2 = not_1_out ? A2 : 1'bz;  // Controlled_Buffer controlled_buffer_2
  assign Y3 = not_1_out ? A3 : 1'bz;  // Controlled_Buffer controlled_buffer_3
  assign Y4 = not_1_out ? A4 : 1'bz;  // Controlled_Buffer controlled_buffer_4
  assign Z1 = not_2_out ? B1 : 1'bz;  // Controlled_Buffer controlled_buffer_5
  assign Z2 = not_2_out ? B2 : 1'bz;  // Controlled_Buffer controlled_buffer_6
  assign Z3 = not_2_out ? B3 : 1'bz;  // Controlled_Buffer controlled_buffer_7
  assign Z4 = not_2_out ? B4 : 1'bz;  // Controlled_Buffer controlled_buffer_8
endmodule

module IC_74273 (
  input  D1,
  input  D2,
  input  D3,
  input  D4,
  input  D5,
  input  D6,
  input  D7,
  input  D8,
  input  CLK,
  input  CLR,
  output Y1,
  output Y2,
  output Y3,
  output Y4,
  output Y5,
  output Y6,
  output Y7,
  output Y8
);

  wire not_1_out;

  not not_1 (not_1_out, CLR);
  D_Flip_Flop d_flip_flop_1 (.D(D1), .CLK(CLK), .Q(Y1), .CLR(not_1_out));  // open: R, SET
  D_Flip_Flop d_flip_flop_2 (.D(D2), .CLK(CLK), .Q(Y2), .CLR(not_1_out));  // open: R, SET
  D_Flip_Flop d_flip_flop_3 (.D(D3), .CLK(CLK), .Q(Y3), .CLR(not_1_out));  // open: R, SET
  D_Flip_Flop d_flip_flop_4 (.D(D4), .CLK(CLK), .Q(Y4), .CLR(not_1_out));  // open: R, SET
  D_Flip_Flop d_flip_flop_5 (.D(D5), .CLK(CLK), .Q(Y5), .CLR(not_1_out));  // open: R, SET
  D_Flip_Flop d_flip_flop_6 (.D(D6), .CLK(CLK), .Q(Y6), .CLR(not_1_out));  // open: R, SET
  D_Flip_Flop d_flip_flop_7 (.D(D7), .CLK(CLK), .Q(Y7), .CLR(not_1_out));  // open: R, SET
  D_Flip_Flop d_flip_flop_8 (.D(D8), .CLK(CLK), .Q(Y8), .CLR(not_1_out));  // open: R, SET
endmodule

module IC_74283 (
  input  A1,
  input  A2,
  input  A3,
  input  A4,
  input  B1,
  input  B2,
  input  B3,
  input  B4,
  input  CIN,
  output Y1,
  output Y2,
  output Y3,
  output Y4,
  output COUT
);

  wire and_1_out, and_2_out, and_3_out, and_4_out, and_5_out, and_6_out, and_7_out, and_8_out, and_9_out,
       and_10_out, and_11_out, and_12_out, and_13_out, and_14_out, nand_1_out, nand_2_out, nand_3_out,
       nand_4_out, nor_1_out, nor_2_out, nor_3_out, nor_4_out, nor_5_out, nor_6_out, nor_7_out, not_1_out,
       not_2_out, not_3_out, not_4_out, not_5_out, not_6_out;

  not not_1 (not_1_out, CIN);
  nor nor_1 (nor_1_out, A1, B1);
  nand nand_1 (nand_1_out, A1, B1);
  nor nor_2 (nor_2_out, A2, B2);
  nand nand_2 (nand_2_out, A2, B2);
  nor nor_3 (nor_3_out, A3, B3);
  nand nand_3 (nand_3_out, A3, B3);
  nor nor_4 (nor_4_out, A4, B4);
  nand nand_4 (nand_4_out, A4, B4);
  not not_2 (not_2_out, not_1_out);
  not not_3 (not_3_out, nor_1_out);
  and and_1 (and_1_out, not_1_out, nand_1_out);
  not not_4 (not_4_out, nor_2_out);
  and and_2 (and_2_out, not_1_out, nand_1_out, nand_2_out);
  and and_3 (and_3_out, nand_2_out, nor_1_out);
  not not_5 (not_5_out, nor_3_out);
  and and_4 (and_4_out, not_1_out, nand_1_out, nand_2_out, nand_3_out);
  and and_5 (and_5_out, nand_2_out, nand_3_out, nor_1_out);
  and and_6 (and_6_out, nand_3_out, nor_2_out);
  not not_6 (not_6_out, nor_4_out);
  and and_7 (and_7_out, not_1_out, nand_1_out, nand_2_out, nand_3_out, nand_4_out);
  and and_8 (and_8_out, nand_2_out, nand_3_out, nand_4_out, nor_1_out);
  and and_9 (and_9_out, nand_3_out, nand_4_out, nor_2_out);
  and and_10 (and_10_out, nand_4_out, nor_3_out);
  and and_11 (and_11_out, not_3_out, nand_1_out);
  nor nor_5 (nor_5_out, and_1_out, nor_1_out);
  and and_12 (and_12_out, not_4_out, nand_2_out);
  nor nor_6 (nor_6_out, and_2_out, and_3_out, nor_2_out);
  and and_13 (and_13_out, not_5_out, nand_3_out);
  nor nor_7 (nor_7_out, and_4_out, and_5_out, and_6_out, nor_3_out);
  and and_14 (and_14_out, not_6_out, nand_4_out);
  nor nor_8 (COUT, and_7_out, and_8_out, and_9_out, and_10_out, nor_4_out);
  xor xor_1 (Y1, not_2_out, and_11_out);
  xor xor_2 (Y2, nor_5_out, and_12_out);
  xor xor_3 (Y3, nor_6_out, and_13_out);
  xor xor_4 (Y4, nor_7_out, and_14_out);
endmodule

module IC_74374 (
  input  D1,
  input  D2,
  input  D3,
  input  D4,
  input  D5,
  input  D6,
  input  D7,
  input  D8,
  input  CLK,
  input  OE,
  output Y1,
  output Y2,
  output Y3,
  output Y4,
  output Y5,
  output Y6,
  output Y7,
  output Y8
);

  wire d_flip_flop_1_q, d_flip_flop_2_q, d_flip_flop_3_q, d_flip_flop_4_q, d_flip_flop_5_q, d_flip_flop_6_q,
       d_flip_flop_7_q, d_flip_flop_8_q, not_1_out;

  D_Flip_Flop d_flip_flop_1 (.D(D1), .CLK(CLK), .Q(d_flip_flop_1_q));  // open: R, SET, CLR
  D_Flip_Flop d_flip_flop_2 (.D(D2), .CLK(CLK), .Q(d_flip_flop_2_q));  // open: R, SET, CLR
  D_Flip_Flop d_flip_flop_3 (.D(D3), .CLK(CLK), .Q(d_flip_flop_3_q));  // open: R, SET, CLR
  D_Flip_Flop d_flip_flop_4 (.D(D4), .CLK(CLK), .Q(d_flip_flop_4_q));  // open: R, SET, CLR
  D_Flip_Flop d_flip_flop_5 (.D(D5), .CLK(CLK), .Q(d_flip_flop_5_q));  // open: R, SET, CLR
  D_Flip_Flop d_flip_flop_6 (.D(D6), .CLK(CLK), .Q(d_flip_flop_6_q));  // open: R, SET, CLR
  D_Flip_Flop d_flip_flop_7 (.D(D7), .CLK(CLK), .Q(d_flip_flop_7_q));  // open: R, SET, CLR
  D_Flip_Flop d_flip_flop_8 (.D(D8), .CLK(CLK), .Q(d_flip_flop_8_q));  // open: R, SET, CLR
  not not_1 (not_1_out, OE);
  assign Y1 = not_1_out ? d_flip_flop_1_q : 1'bz;  // Controlled_Buffer controlled_buffer_1
  assign Y2 = not_1_out ? d_flip_flop_2_q : 1'bz;  // Controlled_Buffer controlled_buffer_2
  assign Y3 = not_1_out ? d_flip_flop_3_q : 1'bz;  // Controlled_Buffer controlled_buffer_3
  assign Y4 = not_1_out ? d_flip_flop_4_q : 1'bz;  // Controlled_Buffer controlled_buffer_4
  assign Y5 = not_1_out ? d_flip_flop_5_q : 1'bz;  // Controlled_Buffer controlled_buffer_5
  assign Y6 = not_1_out ? d_flip_flop_6_q : 1'bz;  // Controlled_Buffer controlled_buffer_6
  assign Y7 = not_1_out ? d_flip_flop_7_q : 1'bz;  // Controlled_Buffer controlled_buffer_7
  assign Y8 = not_1_out ? d_flip_flop_8_q : 1'bz;  // Controlled_Buffer controlled_buffer_8
endmodule

module IC_74377 (
  input  D1,
  input  D2,
  input  D3,
  input  D4,
  input  D5,
  input  D6,
  input  D7,
  input  D8,
  input  CLK,
  input  CE,
  output Y1,
  output Y2,
  output Y3,
  output Y4,
  output Y5,
  output Y6,
  output Y7,
  output Y8
);

  wire and_1_out, not_1_out;

  not not_1 (not_1_out, CE);
  and and_1 (and_1_out, CLK, not_1_out);
  D_Flip_Flop d_flip_flop_1 (.D(D1), .CLK(and_1_out), .Q(Y1));  // open: R, SET, CLR
  D_Flip_Flop d_flip_flop_2 (.D(D2), .CLK(and_1_out), .Q(Y2));  // open: R, SET, CLR
  D_Flip_Flop d_flip_flop_3 (.D(D3), .CLK(and_1_out), .Q(Y3));  // open: R, SET, CLR
  D_Flip_Flop d_flip_flop_4 (.D(D4), .CLK(and_1_out), .Q(Y4));  // open: R, SET, CLR
  D_Flip_Flop d_flip_flop_5 (.D(D5), .CLK(and_1_out), .Q(Y5));  // open: R, SET, CLR
  D_Flip_Flop d_flip_flop_6 (.D(D6), .CLK(and_1_out), .Q(Y6));  // open: R, SET, CLR
  D_Flip_Flop d_flip_flop_7 (.D(D7), .CLK(and_1_out), .Q(Y7));  // open: R, SET, CLR
  D_Flip_Flop d_flip_flop_8 (.D(D8), .CLK(and_1_out), .Q(Y8));  // open: R, SET, CLR
endmodule

module D_Flip_Flop (
  input  SET,
  input  D,
  input  CLK,
  input  CLR,
  output Q,
  output R
);

  D_Flip_Flop_part d_ff_1 (.clk(CLK), .D(D), .Q(Q), .Qn(R), .preset(SET), .reset(CLR));  // open: en
endmodule

module D_Latch (
  input  SET,
  input  D,
  input  LE,
  input  CLR,
  output Q,
  output R
);

  D_Flip_Flop_part #(.trigger("high")) d_ff_1 (.clk(LE), .D(D), .Q(Q), .Qn(R), .preset(SET), .reset(CLR));  // open: en
endmodule

module JK_Flip_Flop (
  input  SET,
  input  J,
  input  CLK,
  input  K,
  input  CLR,
  output Q,
  output R
);

  J_K_Flip_Flop j_k_ff_1 (.J(J), .clk(CLK), .K(K), .Q(Q), .Qn(R), .preset(SET), .reset(CLR));  // open: en

  // Notes on the sheet:
  //   CLR: pull=down
  //   SET: pull=down
endmodule
